// Logisim project bcd7seg.circ as structural Verilog
module bcd7seg (
  input  B0,
  input  B1,
  input  B2,
  input  B3,
  output a,
  output b,
  output c,
  output d,
  output e,
  output f,
  output g
);

  wire TQ0, TQ1, TQ1a, TQ1b, TQ1c, TQ1d, TQ1e, TQ1f, TQ1g, TQ1h, TQ1i, TQ1j, TQ1k, TQ1l, TQ1m, TQ1n, TQ1o,
       TQ1q, TQ1r, TQ1s, TQ1t, TQ1u, TQ1v, TQ1w, TQ1x, TQ1y, TQ1z, TQ2, TQ2a, TQ2b, TQ2c, TQ2d, TQ2e, TQ2f,
       TQ2g, TQ2h, TQ2i, TQ2j, TQ2k, TQ2l, TQ2m, TQ2n, TQ2p, TQ2q, TQ2r, TQ2s, TQ2t, TQ2u, TQ2v, TQ2w, TQ2x,
       TQ2y, TQ2z, TQ3, TQ3a, TQ3b, TQ3c, TQ3d, TQ3e, TQ3g, TQ3h, TQ3i, TQ3j, TQ3k, TQ3l, TQ3m, TQ3n, TQ3o,
       TQ3p, TQ3q, TQ3r, TQ3s, TQ3t, TQ3v, TQ3w, TQ3x, TQ3y, TQ3z, TQ4, TQ4a, TQ4b, TQ4c, TQ4d, TQ4e, TQ4f,
       TQ4g, TQ4i, TQ4j, TQ4k, TQ4l, TQ4m, TQ4n, TQ4o, TQ4p, TQ4q, TQ4r, TQ4s, TQ4t, TQ4u, TQ4v, TQ4x, TQ4z,
       TQ5, TQ5a, TQ5b, TQ5c, TQ5e, TQ5f, TQ6, TQ7, TQ8, TQ9, TQ10, TQ11, TQ12, TQ13, TQ14, TQ15, TQ16, TQ17,
       TQ18, TQ19, TQ20, TQ21, TQ22, TQ23, TQ24, TQ25, TQ26, TQ27, TQ28, TQ29, TQ30, TQ31, TQ32, TQ33, TQ34,
       TQ35, TQ36, TQ37, TQ38, TQ39, TQ40, TQ41, TQ42, TQ43, TQ44, TQ45, TQ46, TQ47, TQ48, TQ49, TQ50, TQ51,
       TQ52, TQ53, TQ54, TQ55, TQ56, TQ57, TQ59, TQa, TQb, TQc, TQd, TQe, TQf, TQg, TQh, TQi, TQj, TQk, TQl,
       TQm, TQn, TQo, TQp, TQq, TQr, TQs, TQt, TQv, TQw, TQx, TQy, TQz;

  not B7N1 (TQ53, B0);
  and B7P9 (TQ7, TQ6, TQ5b);
  and B7P21 (TQj, TQi, B2);
  and B7P33 (TQw, TQv, TQ5b);
  and B7P45 (TQ18, TQ16, TQ50);
  and B7P57 (TQ1k, TQ1i, B3);
  or B7O69 (TQ1y, TQ1u, TQ1v);
  or B7O81 (TQ2a, TQ26, TQ27);
  or B7O93 (TQ2m, TQ2i, TQ2j);
  and B7P105 (TQ2v, B0, B1);
  and B7P117 (TQ37, TQ53, TQ59);
  and B7P129 (TQ3j, TQ3i, TQ5b);
  and B7P141 (TQ3w, TQ3v, TQ5b);
  and B7P153 (TQ48, TQ46, TQ50);
  and B7P165 (TQ4m, TQ4j, TQ50);
  or B7O177 (TQ51, TQ4u, TQ4v);
  or B7O189 (g, TQ5e, TQ5f);
  not B7N2 (TQ59, B1);
  and B7P10 (TQ9, TQ7, TQ50);
  and B7P22 (TQl, TQj, TQ50);
  and B7P34 (TQz, TQw, TQ50);
  or B7O46 (TQ1b, TQ17, TQ18);
  or B7O58 (TQ1n, TQ1j, TQ1k);
  and B7P70 (TQ1w, B0, B1);
  and B7P82 (TQ28, TQ53, B1);
  and B7P94 (TQ2k, B0, TQ59);
  and B7P106 (TQ2w, TQ2v, TQ5b);
  and B7P118 (TQ38, TQ37, TQ5b);
  and B7P130 (TQ3l, TQ3j, TQ50);
  and B7P142 (TQ3z, TQ3w, TQ50);
  or B7O154 (TQ4b, TQ47, TQ48);
  and B7P166 (TQ4k, B0, B1);
  and B7P178 (TQ4x, TQ53, B1);
  not B7N3 (TQ5b, B2);
  not B7N4 (TQ50, B3);
  or B7O11 (TQc, TQ8, TQ9);
  or B7O23 (TQo, TQk, TQl);
  and B7P35 (TQx, B0, TQ59);
  and B7P47 (TQ19, TQ53, TQ59);
  and B7P59 (TQ1l, B0, TQ59);
  and B7P71 (TQ1x, TQ1w, TQ5b);
  and B7P83 (TQ29, TQ28, B2);
  and B7P95 (TQ2l, TQ2k, TQ5b);
  and B7P107 (TQ2y, TQ2w, TQ50);
  and B7P119 (TQ3a, TQ38, B3);
  or B7O131 (TQ3o, TQ3k, TQ3l);
  and B7P143 (TQ3x, TQ53, TQ59);
  and B7P155 (TQ49, TQ53, TQ59);
  and B7P167 (TQ4l, TQ4k, TQ5b);
  and B7P179 (TQ4z, TQ4x, B2);
  and B7P1 (TQ0, TQ53, TQ59);
  and B7P12 (TQa, B0, TQ59);
  and B7P24 (TQm, TQ53, TQ59);
  and B7P36 (TQy, TQx, TQ5b);
  and B7P48 (TQ1a, TQ19, B2);
  and B7P60 (TQ1m, TQ1l, TQ5b);
  and B7P72 (TQ1z, TQ1x, TQ50);
  and B7P84 (TQ2b, TQ29, TQ50);
  and B7P96 (TQ2n, TQ2l, B3);
  or B7O108 (TQ31, TQ2x, TQ2y);
  or B7O120 (TQ3d, TQ39, TQ3a);
  and B7P132 (TQ3m, TQ53, B1);
  and B7P144 (TQ3y, TQ3x, B2);
  and B7P156 (TQ4a, TQ49, TQ5b);
  and B7P168 (TQ4n, TQ4l, TQ50);
  and B7P180 (TQ52, TQ4z, TQ50);
  and B7P2 (TQ1, TQ0, TQ5b);
  and B7P13 (TQb, TQa, B2);
  and B7P25 (TQn, TQm, TQ5b);
  and B7P37 (TQ10, TQy, TQ50);
  and B7P49 (TQ1c, TQ1a, TQ50);
  and B7P61 (TQ1o, TQ1m, B3);
  or B7O73 (TQ22, TQ1y, TQ1z);
  or B7O85 (TQ2e, TQ2a, TQ2b);
  or B7O97 (c, TQ2m, TQ2n);
  and B7P109 (TQ2z, B0, TQ59);
  and B7P121 (TQ3b, B0, TQ59);
  and B7P133 (TQ3n, TQ3m, B2);
  and B7P145 (TQ40, TQ3y, TQ50);
  and B7P157 (TQ4c, TQ4a, B3);
  or B7O169 (TQ4q, TQ4m, TQ4n);
  or B7O181 (TQ56, TQ51, TQ52);
  and B7P3 (TQ4, TQ1, TQ50);
  and B7P14 (TQd, TQb, TQ50);
  and B7P26 (TQp, TQn, B3);
  or B7O38 (TQ13, TQz, TQ10);
  or B7O50 (TQ1f, TQ1b, TQ1c);
  or B7O62 (b, TQ1n, TQ1o);
  and B7P74 (TQ20, TQ53, TQ59);
  and B7P86 (TQ2c, B0, B1);
  and B7P98 (TQ2p, TQ53, TQ59);
  and B7P110 (TQ30, TQ2z, B2);
  and B7P122 (TQ3c, TQ3b, TQ5b);
  and B7P134 (TQ3p, TQ3n, TQ50);
  or B7O146 (TQ43, TQ3z, TQ40);
  or B7O158 (TQ4f, TQ4b, TQ4c);
  and B7P170 (TQ4o, TQ53, TQ59);
  and B7P182 (TQ54, TQ53, TQ59);
  and B7P4 (TQ2, TQ53, B1);
  or B7O15 (TQg, TQc, TQd);
  or B7O27 (TQs, TQo, TQp);
  and B7P39 (TQ11, TQ53, B1);
  and B7P51 (TQ1d, B0, B1);
  and B7P63 (TQ1q, TQ53, TQ59);
  and B7P75 (TQ21, TQ20, B2);
  and B7P87 (TQ2d, TQ2c, B2);
  and B7P99 (TQ2q, TQ2p, TQ5b);
  and B7P111 (TQ32, TQ30, TQ50);
  and B7P123 (TQ3e, TQ3c, B3);
  or B7O135 (TQ3s, TQ3o, TQ3p);
  and B7P147 (TQ41, B0, TQ59);
  and B7P159 (TQ4d, B0, TQ59);
  and B7P171 (TQ4p, TQ4o, B2);
  and B7P183 (TQ55, TQ54, TQ5b);
  and B7P5 (TQ3, TQ2, TQ5b);
  and B7P16 (TQe, TQ53, B1);
  and B7P28 (TQq, B0, TQ59);
  and B7P40 (TQ12, TQ11, TQ5b);
  and B7P52 (TQ1e, TQ1d, B2);
  and B7P64 (TQ1r, TQ1q, TQ5b);
  and B7P76 (TQ23, TQ21, TQ50);
  and B7P88 (TQ2f, TQ2d, TQ50);
  and B7P100 (TQ2t, TQ2q, TQ50);
  or B7O112 (TQ35, TQ31, TQ32);
  or B7O124 (d, TQ3d, TQ3e);
  and B7P136 (TQ3q, TQ53, TQ59);
  and B7P148 (TQ42, TQ41, B2);
  and B7P160 (TQ4e, TQ4d, TQ5b);
  and B7P172 (TQ4r, TQ4p, TQ50);
  and B7P184 (TQ57, TQ55, B3);
  and B7P6 (TQ5, TQ3, TQ50);
  and B7P17 (TQf, TQe, B2);
  and B7P29 (TQr, TQq, TQ5b);
  and B7P41 (TQ14, TQ12, TQ50);
  and B7P53 (TQ1g, TQ1e, TQ50);
  and B7P65 (TQ1u, TQ1r, TQ50);
  or B7O77 (TQ26, TQ22, TQ23);
  or B7O89 (TQ2i, TQ2e, TQ2f);
  and B7P101 (TQ2r, TQ53, B1);
  and B7P113 (TQ33, TQ53, B1);
  and B7P125 (TQ3g, TQ53, TQ59);
  and B7P137 (TQ3r, TQ3q, TQ5b);
  and B7P149 (TQ44, TQ42, TQ50);
  and B7P161 (TQ4g, TQ4e, B3);
  or B7O173 (TQ4u, TQ4q, TQ4r);
  or B7O185 (TQ5e, TQ56, TQ57);
  or B7O7 (TQ8, TQ4, TQ5);
  and B7P18 (TQh, TQf, TQ50);
  and B7P30 (TQt, TQr, B3);
  or B7O42 (TQ17, TQ13, TQ14);
  or B7O54 (TQ1j, TQ1f, TQ1g);
  and B7P66 (TQ1s, B0, TQ59);
  and B7P78 (TQ24, B0, TQ59);
  and B7P90 (TQ2g, TQ53, TQ59);
  and B7P102 (TQ2s, TQ2r, TQ5b);
  and B7P114 (TQ34, TQ33, B2);
  and B7P126 (TQ3h, TQ3g, TQ5b);
  and B7P138 (TQ3t, TQ3r, B3);
  or B7O150 (TQ47, TQ43, TQ44);
  or B7O162 (f, TQ4f, TQ4g);
  and B7P174 (TQ4s, B0, TQ59);
  and B7P186 (TQ5a, B0, TQ59);
  and B7P8 (TQ6, B0, B1);
  or B7O19 (TQk, TQg, TQh);
  or B7O31 (a, TQs, TQt);
  and B7P43 (TQ15, B0, B1);
  and B7P55 (TQ1h, TQ53, TQ59);
  and B7P67 (TQ1t, TQ1s, TQ5b);
  and B7P79 (TQ25, TQ24, B2);
  and B7P91 (TQ2h, TQ2g, TQ5b);
  and B7P103 (TQ2u, TQ2s, TQ50);
  and B7P115 (TQ36, TQ34, TQ50);
  and B7P127 (TQ3k, TQ3h, TQ50);
  or B7O139 (e, TQ3s, TQ3t);
  and B7P151 (TQ45, TQ53, B1);
  and B7P163 (TQ4i, TQ53, B1);
  and B7P175 (TQ4t, TQ4s, B2);
  and B7P187 (TQ5c, TQ5a, TQ5b);
  and B7P20 (TQi, B0, B1);
  and B7P32 (TQv, TQ53, TQ59);
  and B7P44 (TQ16, TQ15, TQ5b);
  and B7P56 (TQ1i, TQ1h, TQ5b);
  and B7P68 (TQ1v, TQ1t, TQ50);
  and B7P80 (TQ27, TQ25, TQ50);
  and B7P92 (TQ2j, TQ2h, B3);
  or B7O104 (TQ2x, TQ2t, TQ2u);
  or B7O116 (TQ39, TQ35, TQ36);
  and B7P128 (TQ3i, TQ53, B1);
  and B7P140 (TQ3v, TQ53, TQ59);
  and B7P152 (TQ46, TQ45, B2);
  and B7P164 (TQ4j, TQ4i, TQ5b);
  and B7P176 (TQ4v, TQ4t, TQ50);
  and B7P188 (TQ5f, TQ5c, B3);

  // Other names for the same wires on the sheet: TQ1p = b; TQ2o = c; TQ3f = d; TQ3u = e; TQ4h = f; TQ4w = B1;
  //   TQ4y = B2; TQ5d = B3; TQ5g = g; TQ58 = B0; TQu = a
endmodule
