// Logisim project bcd_subtractor.circ as structural Verilog
module bcd_subtractor (
  input  A0,
  input  B0,
  input  A1,
  input  B1,
  input  A2,
  input  B2,
  input  A3,
  input  B3,
  input  GND,
  input  ONE,
  output D0,
  output D1,
  output D2,
  output D3,
  output Borrow
);

  wire A11_out, A12_out, A13_out, A14_out, A31_out, A32_out, A33_out, A34_out, A41_out, A42_out, A43_out,
       A44_out, B2J9_out, B2K9_out, B2L9_out, B2T10_out, B11_out, B12_out, B13_out, B14_out, B31_out,
       B32_out, B33_out, B34_out, B41_out, B42_out, B43_out, B44_out, C11_out, C12_out, C13_out, C14_out,
       C31_out, C32_out, C33_out, C34_out, C41_out, C42_out, C43_out, C44_out, G11_out, G12_out, G13_out,
       G14_out, G31_out, G32_out, G33_out, G34_out, G41_out, G42_out, G43_out, N1_out, N2_out, O1_out,
       S11_out, S12_out, S13_out, S14_out, S31_out, S32_out, S33_out, S34_out, X2_out, X3_out, X11_out,
       X12_out, X13_out, X14_out, X31_out, X32_out, X33_out, X34_out, X41_out, X42_out, X43_out, X44_out;

  not N1 (N1_out, B0);
  xor X2 (X2_out, B2, B1);
  or O1 (O1_out, B2, B1);
  xor X3 (X3_out, B3, O1_out);
  not N2 (N2_out, X3_out);
  xor X11 (X11_out, A0, N1_out);
  xor S11 (S11_out, X11_out, GND);
  and A11 (A11_out, A0, N1_out);
  and B11 (B11_out, GND, X11_out);
  or C11 (C11_out, A11_out, B11_out);
  or G11 (G11_out, C11_out, GND);
  xor X12 (X12_out, A1, B1);
  xor S12 (S12_out, X12_out, G11_out);
  and A12 (A12_out, A1, B1);
  and B12 (B12_out, G11_out, X12_out);
  or C12 (C12_out, A12_out, B12_out);
  or G12 (G12_out, C12_out, GND);
  xor X13 (X13_out, A2, X2_out);
  xor S13 (S13_out, X13_out, G12_out);
  and A13 (A13_out, A2, X2_out);
  and B13 (B13_out, G12_out, X13_out);
  or C13 (C13_out, A13_out, B13_out);
  or G13 (G13_out, C13_out, GND);
  xor X14 (X14_out, A3, N2_out);
  xor S14 (S14_out, X14_out, G13_out);
  and A14 (A14_out, A3, N2_out);
  and B14 (B14_out, G13_out, X14_out);
  or C14 (C14_out, A14_out, B14_out);
  or G14 (G14_out, C14_out, GND);
  xor X31 (X31_out, S11_out, ONE);
  xor S31 (S31_out, X31_out, GND);
  and A31 (A31_out, S11_out, ONE);
  and B31 (B31_out, GND, X31_out);
  or C31 (C31_out, A31_out, B31_out);
  or G31 (G31_out, C31_out, GND);
  xor X32 (X32_out, S12_out, GND);
  xor S32 (S32_out, X32_out, G31_out);
  and A32 (A32_out, S12_out, GND);
  and B32 (B32_out, G31_out, X32_out);
  or C32 (C32_out, A32_out, B32_out);
  or G32 (G32_out, C32_out, GND);
  xor X33 (X33_out, S13_out, GND);
  xor S33 (S33_out, X33_out, G32_out);
  and A33 (A33_out, S13_out, GND);
  and B33 (B33_out, G32_out, X33_out);
  or C33 (C33_out, A33_out, B33_out);
  or G33 (G33_out, C33_out, GND);
  xor X34 (X34_out, S14_out, GND);
  xor S34 (S34_out, X34_out, G33_out);
  and A34 (A34_out, S14_out, GND);
  and B34 (B34_out, G33_out, X34_out);
  or C34 (C34_out, A34_out, B34_out);
  or G34 (G34_out, C34_out, GND);
  or B2J9 (B2J9_out, B2T10_out, B2K9_out);
  and B2K9 (B2K9_out, B2L9_out, S34_out);
  or B2L9 (B2L9_out, S33_out, S32_out);
  or B2T10 (B2T10_out, G14_out, G34_out);
  xor X41 (X41_out, S31_out, GND);
  xor S41 (D0, X41_out, GND);
  and A41 (A41_out, S31_out, GND);
  and B41 (B41_out, GND, X41_out);
  or C41 (C41_out, A41_out, B41_out);
  or G41 (G41_out, C41_out, GND);
  xor X42 (X42_out, S32_out, B2J9_out);
  xor S42 (D1, X42_out, G41_out);
  and A42 (A42_out, S32_out, B2J9_out);
  and B42 (B42_out, G41_out, X42_out);
  or C42 (C42_out, A42_out, B42_out);
  or G42 (G42_out, C42_out, GND);
  xor X43 (X43_out, S33_out, B2J9_out);
  xor S43 (D2, X43_out, G42_out);
  and A43 (A43_out, S33_out, B2J9_out);
  and B43 (B43_out, G42_out, X43_out);
  or C43 (C43_out, A43_out, B43_out);
  or G43 (G43_out, C43_out, GND);
  xor X44 (X44_out, S34_out, GND);
  xor S44 (D3, X44_out, G43_out);
  and A44 (A44_out, S34_out, GND);
  and B44 (B44_out, G43_out, X44_out);
  or C44 (C44_out, A44_out, B44_out);
  // OR_Gate G44 has open pins: in0=C44_out, in1=GND, out=open
  not NB (Borrow, B2J9_out);
endmodule
