// Logisim project bcd_subtractor_2digit.circ as structural Verilog
module bcd_subtractor_2digit (
  input  A0,
  input  B0,
  input  A1,
  input  B1,
  input  A2,
  input  B2,
  input  A3,
  input  B3,
  input  A4,
  input  B4,
  input  A5,
  input  B5,
  input  A6,
  input  B6,
  input  A7,
  input  B7,
  input  Bin,
  input  GND,
  output D0,
  output D1,
  output D2,
  output D3,
  output D4,
  output D5,
  output D6,
  output D7,
  output Borrow
);

  wire A43_out, A44_out, and_24_out, B43_out, C42_out, G42_out, G43_out, or_23_out, or_24_out, TQ1, TQ1a,
       TQ1c, TQ1d, TQ1e, TQ1f, TQ1g, TQ1h, TQ1j, TQ1k, TQ1l, TQ1m, TQ1n, TQ1o, TQ1q, TQ1r, TQ1y, TQ2a, TQ2b,
       TQ2c, TQ2d, TQ2e, TQ2f, TQ2g, TQ2h, TQ2i, TQ2j, TQ2k, TQ2l, TQ2m, TQ2n, TQ2o, TQ2p, TQ2q, TQ2r, TQ2s,
       TQ2t, TQ2u, TQ2v, TQ2w, TQ2x, TQ2y, TQ2z, TQ3, TQ3a, TQ3b, TQ3f, TQ3g, TQ3i, TQ3j, TQ3k, TQ3l, TQ3m,
       TQ3p, TQ3q, TQ3r, TQ3s, TQ3t, TQ3v, TQ3w, TQ3x, TQ3y, TQ3z, TQ4a, TQ4b, TQ4c, TQ4d, TQ4e, TQ4f, TQ4g,
       TQ4h, TQ4i, TQ4j, TQ4k, TQ4l, TQ4m, TQ4n, TQ4o, TQ4p, TQ4q, TQ5, TQ6, TQ7, TQ8, TQ9, TQ10, TQ11, TQ12,
       TQ13, TQ14, TQ15, TQ16, TQ17, TQ18, TQ19, TQ21, TQ23, TQ24, TQ25, TQ26, TQ27, TQ28, TQ29, TQ30, TQ31,
       TQ32, TQ33, TQ34, TQ35, TQ36, TQ37, TQ38, TQ39, TQ40, TQ42, TQ43, TQ44, TQ45, TQ46, TQ47, TQ48, TQ49,
       TQa, TQc, TQd, TQe, TQf, TQg, TQh, TQi, TQj, TQk, TQl, TQm, TQp, TQq, TQr, TQs, TQt, TQu, TQv, TQw,
       TQx, TQy, X43_out, xor_25_out;

  not not_1 (TQd, B0);
  xor X2 (TQ11, B2, B1);
  or O1 (TQ6, B2, B1);
  xor xor_1 (TQ8, B3, TQ6);
  not not_2 (TQ1c, TQ8);
  xor X11 (TQf, A0, TQd);
  xor S11 (TQ1k, TQf, GND);
  and A11 (TQh, A0, TQd);
  and and_1 (TQj, GND, TQf);
  or C11 (TQl, TQh, TQj);
  or G11 (TQq, TQl, GND);
  xor xor_2 (TQs, A1, B1);
  xor S12 (TQ1y, TQs, TQq);
  and and_2 (TQu, A1, B1);
  and B12 (TQw, TQq, TQs);
  or or_1 (TQx, TQu, TQw);
  or or_2 (TQ13, TQx, GND);
  xor X13 (TQ15, A2, TQ11);
  xor xor_3 (TQ27, TQ15, TQ13);
  and and_3 (TQ17, A2, TQ11);
  and B13 (TQ18, TQ13, TQ15);
  or or_3 (TQ19, TQ17, TQ18);
  or or_4 (TQ1d, TQ19, GND);
  xor X14 (TQ1e, A3, TQ1c);
  xor xor_4 (TQ2d, TQ1e, TQ1d);
  and and_4 (TQ1f, A3, TQ1c);
  and and_5 (TQ1g, TQ1d, TQ1e);
  or C14 (TQ1h, TQ1f, TQ1g);
  or G14 (TQ2k, TQ1h, GND);
  not not_3 (TQ1l, Bin);
  xor xor_5 (TQ1m, TQ1k, TQ1l);
  xor S31 (TQ2o, TQ1m, GND);
  and A31 (TQ1n, TQ1k, TQ1l);
  and and_6 (TQ1o, GND, TQ1m);
  or or_5 (TQ1r, TQ1n, TQ1o);
  or or_6 (TQ21, TQ1r, GND);
  xor X32 (TQ23, TQ1y, GND);
  xor S32 (TQ2t, TQ23, TQ21);
  and A32 (TQ24, TQ1y, GND);
  and and_7 (TQ25, TQ21, TQ23);
  or C32 (TQ26, TQ24, TQ25);
  or G32 (TQ28, TQ26, GND);
  xor X33 (TQ29, TQ27, GND);
  xor S33 (TQ2z, TQ29, TQ28);
  and A33 (TQ2a, TQ27, GND);
  and B33 (TQ2b, TQ28, TQ29);
  or or_7 (TQ2c, TQ2a, TQ2b);
  or or_8 (TQ2e, TQ2c, GND);
  xor X34 (TQ2f, TQ2d, GND);
  xor S34 (TQ35, TQ2f, TQ2e);
  and A34 (TQ2g, TQ2d, GND);
  and B34 (TQ2h, TQ2e, TQ2f);
  or C34 (TQ2i, TQ2g, TQ2h);
  or or_9 (TQ2l, TQ2i, GND);
  or B2J9 (TQ3b, TQ2m, TQ2n);
  and B2K9 (TQ2n, TQ2j, TQ35);
  or B2L9 (TQ2j, TQ2z, TQ2t);
  or B2T9 (TQ2m, TQ2k, TQ2l);
  xor xor_6 (TQ2p, TQ2o, GND);
  xor S41 (D0, TQ2p, GND);
  and A41 (TQ2q, TQ2o, GND);
  and and_8 (TQ2r, GND, TQ2p);
  or or_10 (TQ2s, TQ2q, TQ2r);
  or G41 (TQ2u, TQ2s, GND);
  xor xor_7 (TQ2v, TQ2t, TQ3b);
  xor S42 (D1, TQ2v, TQ2u);
  and A42 (TQ2w, TQ2t, TQ3b);
  and B42 (TQ2x, TQ2u, TQ2v);
  or or_11 (TQ2y, TQ2w, TQ2x);
  or or_12 (TQ30, TQ2y, GND);
  xor xor_8 (TQ31, TQ2z, TQ3b);
  xor xor_9 (D2, TQ31, TQ30);
  and and_9 (TQ32, TQ2z, TQ3b);
  and and_10 (TQ33, TQ30, TQ31);
  or C43 (TQ34, TQ32, TQ33);
  or or_13 (TQ36, TQ34, GND);
  xor X44 (TQ37, TQ35, GND);
  xor S44 (D3, TQ37, TQ36);
  and and_11 (TQ38, TQ35, GND);
  and B44 (TQ39, TQ36, TQ37);
  or C44 (TQ3a, TQ38, TQ39);
  // OR_Gate G44 has open pins: in0=TQ3a, in1=GND, out=open
  not not_4 (TQ48, TQ3b);
  not N1 (TQ3i, B4);
  xor xor_10 (TQ3v, B6, B5);
  or or_14 (TQ3f, B6, B5);
  xor X3 (TQ3g, B7, TQ3f);
  not N2 (TQ42, TQ3g);
  xor xor_11 (TQ3j, A4, TQ3i);
  xor xor_12 (TQ49, TQ3j, GND);
  and and_12 (TQ3k, A4, TQ3i);
  and B11 (TQ3l, GND, TQ3j);
  or or_15 (TQ3m, TQ3k, TQ3l);
  or or_16 (TQ3p, TQ3m, GND);
  xor X12 (TQ3q, A5, B5);
  xor xor_13 (TQ4f, TQ3q, TQ3p);
  and A12 (TQ3r, A5, B5);
  and and_13 (TQ3s, TQ3p, TQ3q);
  or C12 (TQ3t, TQ3r, TQ3s);
  or G12 (TQ3w, TQ3t, GND);
  xor xor_14 (TQ3x, A6, TQ3v);
  xor S13 (TQ4l, TQ3x, TQ3w);
  and A13 (TQ3y, A6, TQ3v);
  and and_14 (TQ3z, TQ3w, TQ3x);
  or C13 (TQ40, TQ3y, TQ3z);
  or G13 (TQ43, TQ40, GND);
  xor xor_15 (TQ44, A7, TQ42);
  xor S14 (TQ1, TQ44, TQ43);
  and A14 (TQ45, A7, TQ42);
  and B14 (TQ46, TQ43, TQ44);
  or or_17 (TQ47, TQ45, TQ46);
  or or_18 (TQe, TQ47, GND);
  not NBIN (TQ4a, TQ48);
  xor X31 (TQ4b, TQ49, TQ4a);
  xor xor_16 (TQm, TQ4b, GND);
  and and_15 (TQ4c, TQ49, TQ4a);
  and B31 (TQ4d, GND, TQ4b);
  or C31 (TQ4e, TQ4c, TQ4d);
  or G31 (TQ4g, TQ4e, GND);
  xor xor_17 (TQ4h, TQ4f, GND);
  xor xor_18 (TQy, TQ4h, TQ4g);
  and and_16 (TQ4i, TQ4f, GND);
  and B32 (TQ4j, TQ4g, TQ4h);
  or or_19 (TQ4k, TQ4i, TQ4j);
  or or_20 (TQ4m, TQ4k, GND);
  xor xor_19 (TQ4n, TQ4l, GND);
  xor xor_20 (TQ1a, TQ4n, TQ4m);
  and and_17 (TQ4o, TQ4l, GND);
  and and_18 (TQ4p, TQ4m, TQ4n);
  or C33 (TQ4q, TQ4o, TQ4p);
  or G33 (TQ3, TQ4q, GND);
  xor xor_21 (TQ5, TQ1, GND);
  xor xor_22 (TQ1j, TQ5, TQ3);
  and and_19 (TQ7, TQ1, GND);
  and and_20 (TQ9, TQ3, TQ5);
  or or_21 (TQa, TQ7, TQ9);
  or G34 (TQg, TQa, GND);
  or B2J22 (TQ1q, TQi, TQk);
  and B2K22 (TQk, TQc, TQ1j);
  or B2L22 (TQc, TQ1a, TQy);
  or B2T22 (TQi, TQe, TQg);
  xor X41 (TQp, TQm, GND);
  xor xor_23 (D4, TQp, GND);
  and and_21 (TQr, TQm, GND);
  and B41 (TQt, GND, TQp);
  or C41 (TQv, TQr, TQt);
  or or_22 (TQ10, TQv, GND);
  xor X42 (TQ12, TQy, TQ1q);
  xor xor_24 (D5, TQ12, TQ10);
  and and_22 (TQ14, TQy, TQ1q);
  and and_23 (TQ16, TQ10, TQ12);
  or C42 (C42_out, TQ14, TQ16);
  or G42 (G42_out, C42_out, GND);
  xor X43 (X43_out, TQ1a, TQ1q);
  xor S43 (D6, X43_out, G42_out);
  and A43 (A43_out, TQ1a, TQ1q);
  and B43 (B43_out, G42_out, X43_out);
  or or_23 (or_23_out, A43_out, B43_out);
  or G43 (G43_out, or_23_out, GND);
  xor xor_25 (xor_25_out, TQ1j, GND);
  xor xor_26 (D7, xor_25_out, G43_out);
  and A44 (A44_out, TQ1j, GND);
  and and_24 (and_24_out, G43_out, xor_25_out);
  or or_24 (or_24_out, A44_out, and_24_out);
  // OR_Gate or_25 has open pins: in0=or_24_out, in1=GND, out=open
  not NB (Borrow, TQ1q);

  // Other names for the same wires on the sheet: TQ0 = B0; TQ1b = A3; TQ1i = Bin; TQ1p = GND; TQ1s = D0; TQ1t = D4;
  //   TQ1u = D1; TQ1v = D5; TQ1w = D2; TQ1x = D6; TQ1z = D3; TQ2 = B2; TQ3c = B4; TQ3d = B6; TQ3e = B7; TQ3h = A4;
  //   TQ3n = A5; TQ3o = B5; TQ3u = A6; TQ4 = B3; TQ20 = D7; TQ22 = Borrow; TQ41 = A7; TQb = A0; TQn = A1; TQo = B1;
  //   TQz = A2
endmodule
