// Logisim project comparator_4bit.circ as structural Verilog
module comparator_4bit (
  input  A0,
  input  B0,
  input  A1,
  input  B1,
  input  A2,
  input  B2,
  input  A3,
  input  B3,
  output GT,
  output EQ,
  output LT
);

  wire TQ0, TQ3, TQ6, TQ9, TQc, TQd, TQe, TQf, TQg, TQh, TQi, TQj, TQk, TQl, TQm, TQn, TQo, TQp, TQq, TQr,
       TQs, TQv;

  xnor CMP0E (TQn, A0, B0);
  or CMPO (TQv, GT, EQ);
  and CMPQ2 (TQp, TQn, TQo);
  not CMP0N (TQ0, B0);
  not CMPL (LT, TQv);
  and CMPQ3 (TQr, TQp, TQq);
  and CMP0G (TQj, A0, TQ0);
  and CMPA1 (TQl, TQm, TQj);
  and CMPQ4 (EQ, TQr, TQs);
  xnor CMP1E (TQo, A1, B1);
  or CMPG1 (GT, TQk, TQl);
  not CMP1N (TQ3, B1);
  // AND_Gate CMPE1 has open pins: in0=TQm, in1=TQn, out=open
  and CMP1G (TQf, A1, TQ3);
  and CMPA2 (TQh, TQi, TQf);
  xnor CMP2E (TQq, A2, B2);
  or CMPG2 (TQk, TQg, TQh);
  not CMP2N (TQ6, B2);
  and CMPE2 (TQm, TQi, TQo);
  and CMP2G (TQc, A2, TQ6);
  and CMPA3 (TQe, TQs, TQc);
  xnor CMP3E (TQs, A3, B3);
  or CMPG3 (TQg, TQd, TQe);
  not CMP3N (TQ9, B3);
  and CMPE3 (TQi, TQs, TQq);
  and CMP3G (TQd, A3, TQ9);
  // AND_Gate CMPQ1 is placed but not wired

  // Other names for the same wires on the sheet: TQ1 = A0; TQ2 = B0; TQ4 = A1; TQ5 = B1; TQ7 = A2; TQ8 = B2; TQa = A3;
  //   TQb = B3; TQt = GT; TQu = EQ; TQw = LT
endmodule
