// Logisim project countdown_timer.circ as structural Verilog
module countdown_timer (
  input  CLK,
  input  LOAD,
  input  RST,
  input  D0,
  input  D1,
  input  D2,
  input  D3,
  output Q0,
  output Q1,
  output Q2,
  output Q3,
  output ZERO
);

  wire TQ0, TQ1, TQ2, TQ5, TQ6, TQ7, TQ9, TQ10, TQa, TQb, TQd, TQe, TQf, TQi, TQj, TQk, TQo, TQq, TQs, TQu,
       TQv, TQw, TQx, TQy, TQz;

  not CTDL (TQv, LOAD);
  D_Flip_Flop CTDF0 (.D(TQ7), .clk(CLK), .Q(Q0), .reset(RST));  // open: Qn, preset
  and CTDB3 (TQj, TQv, TQu);
  not CTDN0 (TQw, Q0);
  or CTDM3 (TQk, TQi, TQj);
  not CTDN1 (TQx, Q1);
  and CTDA1 (TQ9, LOAD, D1);
  and CTDZ1 (TQ0, TQw, TQx);
  and CTDB1 (TQa, TQv, TQq);
  xor CTDX3 (TQu, Q3, TQ10);
  D_Flip_Flop CTDF3 (.D(TQk), .clk(CLK), .Q(Q3), .reset(RST));  // open: Qn, preset
  not CTDN2 (TQz, Q2);
  or CTDM1 (TQb, TQ9, TQa);
  and CTDZ2 (TQ1, TQ0, TQz);
  xor CTDX1 (TQq, Q1, TQw);
  and CTDC2 (TQy, TQw, TQx);
  not CTDN3 (TQ2, Q3);
  and CTDZ3 (ZERO, TQ1, TQ2);
  D_Flip_Flop CTDF1 (.D(TQb), .clk(CLK), .Q(Q1), .reset(RST));  // open: Qn, preset
  and CTDC3 (TQ10, TQy, TQz);
  and CTDA0 (TQ5, LOAD, D0);
  and CTDA2 (TQd, LOAD, D2);
  and CTDB0 (TQ6, TQv, TQo);
  and CTDB2 (TQe, TQv, TQs);
  or CTDM0 (TQ7, TQ5, TQ6);
  or CTDM2 (TQf, TQd, TQe);
  xor CTDX0 (TQo, Q0, TQv);
  xor CTDX2 (TQs, Q2, TQy);
  D_Flip_Flop CTDF2 (.D(TQf), .clk(CLK), .Q(Q2), .reset(RST));  // open: Qn, preset
  and CTDA3 (TQi, LOAD, D3);

  // Other names for the same wires on the sheet: TQ3 = ZERO; TQ4 = D0; TQ8 = D1; TQc = D2; TQg = LOAD; TQh = D3;
  //   TQl = CLK; TQm = RST; TQn = Q0; TQp = Q1; TQr = Q2; TQt = Q3
endmodule
