// Logisim project digital_clock.circ as structural Verilog
module digital_clock (
  input  RST,
  output Q0,
  output Q1,
  output Q2,
  output Q3,
  output Q4,
  output Q5,
  output Q6,
  output Q7,
  output Q8,
  output Q9,
  output Q10,
  output Q11,
  output Q12,
  output Q13,
  output Q18,
  output Q19,
  output Q20,
  output Q21,
  output Q22
);

  wire TQ0, TQ1, TQ1a, TQ1b, TQ1c, TQ1d, TQ1e, TQ1f, TQ1g, TQ1h, TQ1i, TQ1p, TQ1r, TQ1s, TQ1v, TQ1w, TQ1x,
       TQ1y, TQ1z, TQ2, TQ2d, TQ2e, TQ2f, TQ2g, TQ2h, TQ2i, TQ3, TQ4, TQ5, TQ6, TQ7, TQ8, TQ9, TQ10, TQ11,
       TQ12, TQ13, TQ14, TQ15, TQ16, TQ17, TQ18, TQ19, TQ20, TQ21, TQ22, TQ23, TQ24, TQ25, TQ26, TQ27, TQ28,
       TQa, TQb, TQe, TQf, TQh, TQi, TQj, TQk, TQl, TQm, TQn, TQo, TQq, TQr, TQt, TQv, TQx, TQy, TQz;

  Clock CLK (.out(TQ1s));
  T_Flip_Flop D0F0 (.T(TQ9), .clk(TQ1s), .Q(Q0), .reset(RST));  // open: Qn, preset
  and D0R2 (TQf, Q0, Q1);
  not D1NW (TQ14, TQ1r);
  not D2N1 (TQ1v, Q8);
  and D2R3 (TQ25, TQ24, Q9);
  and D3TE (TQ7, TQh, TQ2i);
  and HA1 (TQm, Q18, Q19);
  and HR3 (TQ18, TQ15, Q20);
  and D0M2 (TQe, TQf, TQk);
  and D1TE (TQ1e, TQ1p, TQ14);
  and D2A1 (TQ1w, Q7, TQ1v);
  and D2M3 (TQ27, TQ25, TQ26);
  or D3T0 (TQ0, TQ7, TQj);
  and HA2 (TQo, TQm, Q20);
  and HM3 (TQ17, TQ18, TQ1b);
  T_Flip_Flop D0F1 (.T(TQb), .clk(TQ1s), .Q(Q1), .reset(RST));  // open: Qn, preset
  or D1T0 (TQ16, TQ1e, TQ1r);
  not D2N2 (TQ1x, Q9);
  and D0R3 (TQi, TQf, Q2);
  or D2O3 (TQ28, TQ27, TQ2e);
  and D3M1 (TQ3, Q11, TQ7);
  not HN3 (TQq, Q21);
  and HR4 (TQ1a, TQ18, Q21);
  T_Flip_Flop D0F2 (.T(TQe), .clk(TQ1s), .Q(Q2), .reset(RST));  // open: Qn, preset
  and D0M3 (TQl, TQi, TQk);
  and D1M1 (TQ19, Q4, TQ1e);
  and D2A2 (TQ1y, TQ1w, TQ1x);
  and D2EC (TQh, TQ2d, TQ2e);
  and D3R2 (TQ6, Q11, Q12);
  and HA3 (TQr, TQo, TQq);
  and HM4 (TQ1d, TQ1a, TQ1b);
  and D1R2 (TQ1c, Q4, Q5);
  and D2A3 (TQ1z, TQ1y, Q10);
  and HA4 (TQt, TQr, Q22);
  T_Flip_Flop D0F3 (.T(TQn), .clk(TQ1s), .Q(Q3), .reset(RST));  // open: Qn, preset
  or D0O3 (TQn, TQl, TQ1p);
  T_Flip_Flop D3F0 (.T(TQ0), .clk(TQ1s), .Q(Q11), .reset(RST));  // open: Qn, preset
  and D3M2 (TQ8, TQ6, TQ7);
  or HO4 (TQ1h, TQ1d, TQ1f);
  T_Flip_Flop D1F0 (.T(TQ16), .clk(TQ1s), .Q(Q4), .reset(RST));  // open: Qn, preset
  and D1M2 (TQ1g, TQ1c, TQ1e);
  and D2W (TQ2e, TQ2d, TQ1z);
  or D3O2 (TQa, TQ8, TQj);
  and HW (TQ1f, TQv, TQt);
  not D0N1 (TQ1, Q1);
  or D1O2 (TQ1i, TQ1g, TQ1r);
  not D2NW (TQ20, TQ2e);
  T_Flip_Flop D3F1 (.T(TQ3), .clk(TQ1s), .Q(Q12), .reset(RST));  // open: Qn, preset
  not HNW (TQ1b, TQ1f);
  and D0A1 (TQ2, Q0, TQ1);
  T_Flip_Flop D1F1 (.T(TQ19), .clk(TQ1s), .Q(Q5), .reset(RST));  // open: Qn, preset
  and D2TE (TQ26, TQ2d, TQ20);
  and D3EC (TQv, TQh, TQj);
  and D1EC (TQ2d, TQ1p, TQ1r);
  T_Flip_Flop D3F2 (.T(TQa), .clk(TQ1s), .Q(Q13), .reset(RST));  // open: Qn, preset
  T_Flip_Flop DH0 (.T(TQv), .clk(TQ1s), .Q(Q18), .reset(RST));  // open: Qn, preset
  and HM1 (TQx, Q18, TQ1b);
  not D0N2 (TQ4, Q2);
  T_Flip_Flop D1F2 (.T(TQ1i), .clk(TQ1s), .Q(Q6), .reset(RST));  // open: Qn, preset
  T_Flip_Flop D2F0 (.T(TQ21), .clk(TQ1s), .Q(Q7), .reset(RST));  // open: Qn, preset
  or D2T0 (TQ21, TQ26, TQ2e);
  or HO1 (TQy, TQx, TQ1f);
  and D0A2 (TQ5, TQ2, TQ4);
  and D2M1 (TQ22, Q7, TQ26);
  not D3N1 (TQ2f, Q12);
  T_Flip_Flop DH1 (.T(TQy), .clk(TQ1s), .Q(Q19), .reset(RST));  // open: Qn, preset
  and D0A3 (TQ1p, TQ5, Q3);
  T_Flip_Flop D2F1 (.T(TQ22), .clk(TQ1s), .Q(Q8), .reset(RST));  // open: Qn, preset
  and D3A1 (TQ2g, Q11, TQ2f);
  and HR2 (TQ15, Q18, Q19);
  not D1N1 (TQz, Q5);
  and D2R2 (TQ24, Q7, Q8);
  T_Flip_Flop DH2 (.T(TQ13), .clk(TQ1s), .Q(Q20), .reset(RST));  // open: Qn, preset
  and HM2 (TQ12, TQ15, TQ1b);
  not D0NW (TQk, TQ1p);
  and D1A1 (TQ10, Q4, TQz);
  and D2M2 (TQ23, TQ24, TQ26);
  and D3A2 (TQ2h, TQ2g, Q13);
  or D0T0 (TQ9, TQk, TQ1p);
  and D1A2 (TQ11, TQ10, Q6);
  T_Flip_Flop D2F2 (.T(TQ23), .clk(TQ1s), .Q(Q9), .reset(RST));  // open: Qn, preset
  and D3W (TQj, TQh, TQ2h);
  or HO2 (TQ13, TQ12, TQ1f);
  T_Flip_Flop DH3 (.T(TQ17), .clk(TQ1s), .Q(Q21), .reset(RST));  // open: Qn, preset
  and D0M1 (TQb, Q0, TQk);
  and D1W (TQ1r, TQ1p, TQ11);
  T_Flip_Flop D2F3 (.T(TQ28), .clk(TQ1s), .Q(Q10), .reset(RST));  // open: Qn, preset
  not D3NW (TQ2i, TQj);
  T_Flip_Flop DH4 (.T(TQ1h), .clk(TQ1s), .Q(Q22), .reset(RST));  // open: Qn, preset

  // Other names for the same wires on the sheet: TQ1j = Q18; TQ1k = Q4; TQ1l = Q19; TQ1m = Q5; TQ1n = Q20; TQ1o = Q6;
  //   TQ1q = Q21; TQ1t = RST; TQ1u = Q22; TQ2a = Q8; TQ2b = Q9; TQ2c = Q10; TQ29 = Q7; TQc = Q11; TQd = Q12;
  //   TQg = Q13; TQp = Q0; TQs = Q1; TQu = Q2; TQw = Q3
endmodule
