// Logisim project encoder_8to3.circ as structural Verilog
module encoder_8to3 (
  input  I6,
  input  I7,
  input  I5,
  input  I4,
  input  I3,
  input  I2,
  input  I1,
  input  I0,
  output Y2,
  output Y1,
  output Y0,
  output G
);

  wire TQ0, TQ1, TQ2, TQ3, TQ4, TQ5, TQ7, TQ8, TQa, TQb, TQc, TQd, TQg, TQj, TQk, TQl, TQm, TQn, TQo, TQp,
       TQs, TQt, TQu, TQv, TQw;

  or enc_g_o1 (TQ0, I6, I7);
  not enc_n45 (TQm, TQa);
  and enc_t1b (TQp, TQn, TQo);
  or enc_g_o2 (TQ1, TQ0, I5);
  or enc_r23_o1 (TQb, I3, I2);
  and enc_t1c (TQw, TQp, I1);
  and enc_y1a (TQd, TQm, TQb);
  or enc_g_o3 (TQ2, TQ1, I4);
  or enc_y0a_o1 (TQt, I7, TQs);
  or enc_g_o4 (TQ3, TQ2, I3);
  or enc_y1_o1 (Y1, TQc, TQd);
  or enc_y0b_o1 (TQv, TQt, TQu);
  not enc_n6 (TQo, I6);
  or enc_g_o5 (TQ4, TQ3, I2);
  or enc_y0c_o1 (Y0, TQv, TQw);
  or enc_g_o6 (TQ5, TQ4, I1);
  and enc_t5 (TQs, TQo, I5);
  and enc_t3a (TQg, TQm, TQo);
  or enc_g_o7 (G, TQ5, I0);
  or enc_y2_o1 (TQ7, I4, I5);
  and enc_t3b (TQu, TQg, I3);
  not enc_n2 (TQj, I2);
  or enc_y2_o2 (TQ8, TQ7, I6);
  not enc_n3 (TQk, I3);
  or enc_y2_o3 (Y2, TQ8, I7);
  and enc_n23 (TQl, TQj, TQk);
  or enc_r67_o1 (TQc, I6, I7);
  and enc_t1a (TQn, TQl, TQm);
  or enc_r45_o1 (TQa, I4, I5);

  // Other names for the same wires on the sheet: TQ6 = I0; TQ9 = I4; TQ10 = G; TQe = I6; TQf = I5; TQh = I2; TQi = I3;
  //   TQq = I1; TQr = I7; TQx = Y2; TQy = Y1; TQz = Y0
endmodule
