// Logisim project freq_meter.circ as structural Verilog
module freq_meter (
  input  CLK,
  input  SIG,
  input  RST,
  output F0,
  output F1,
  output F2,
  output F3,
  output WIN
);

  wire TQ0, TQ1, TQ1a, TQ1b, TQ1c, TQ1d, TQ1e, TQ2, TQ3, TQ4, TQ5, TQ6, TQ7, TQ8, TQ9, TQ10, TQ12, TQ13,
       TQ14, TQ15, TQ19, TQb, TQc, TQd, TQe, TQf, TQg, TQh, TQi, TQj, TQk, TQl, TQm, TQn, TQo, TQq, TQr, TQs,
       TQt, TQu, TQv, TQx, TQy, TQz;

  and FW1 (TQ5, TQ3, TQ4);
  not FSPN (TQb, TQ9);
  xor FCX2 (TQj, TQ12, TQl);
  or FLR0 (TQv, TQt, TQu);
  or FLR3 (TQ1e, TQ1c, TQ1d);
  and FW2 (TQ7, TQ5, TQ6);
  and FRIS (TQc, SIG, TQb);
  and FCW2 (TQk, WIN, TQj);
  D_Flip_Flop FLO1 (.D(TQ10), .clk(CLK), .Q(F1), .reset(RST));  // open: Qn, preset
  and FEN (TQf, WIN, TQc);
  D_Flip_Flop FWC0 (.D(TQ0), .clk(CLK), .Q(TQ3), .reset(RST));  // open: Qn, preset
  and FCN2 (TQm, TQl, TQ12);
  and FLA1 (TQy, TQ19, TQx);
  D_Flip_Flop FCC0 (.D(TQe), .clk(CLK), .Q(TQs), .reset(RST));  // open: Qn, preset
  D_Flip_Flop FCC3 (.D(TQo), .clk(CLK), .Q(TQ1a), .reset(RST));  // open: Qn, preset
  D_Flip_Flop FWC1 (.D(TQ1), .clk(CLK), .Q(TQ4), .reset(RST));  // open: Qn, preset
  and FLB1 (TQz, TQ1b, F1);
  xor FCX0 (TQd, TQs, TQf);
  xor FCX3 (TQn, TQ1a, TQm);
  or FLR1 (TQ10, TQy, TQz);
  D_Flip_Flop FWC2 (.D(TQ2), .clk(CLK), .Q(TQ6), .reset(RST));  // open: Qn, preset
  and FCW0 (TQe, WIN, TQd);
  and FCW3 (TQo, WIN, TQn);
  D_Flip_Flop FLO2 (.D(TQ15), .clk(CLK), .Q(F2), .reset(RST));  // open: Qn, preset
  not FWN (TQ0, TQ3);
  and FCN0 (TQi, TQf, TQs);
  not FNW (TQq, WIN);
  xor FWX1 (TQ1, TQ4, TQ3);
  D_Flip_Flop FCC1 (.D(TQh), .clk(CLK), .Q(TQx), .reset(RST));  // open: Qn, preset
  and FLN (TQ19, TQq, TQr);
  and FLA2 (TQ13, TQ19, TQ12);
  and FLB2 (TQ14, TQ1b, F2);
  xor FWX2 (TQ2, TQ6, TQ5);
  not FNL (TQ1b, TQ19);
  D_Flip_Flop FWIN (.D(TQ8), .clk(CLK), .Q(WIN), .reset(RST));  // open: Qn, preset
  xor FCX1 (TQg, TQx, TQi);
  D_Flip_Flop FLO0 (.D(TQv), .clk(CLK), .Q(F0), .reset(RST));  // open: Qn, preset
  or FLR2 (TQ15, TQ13, TQ14);
  and FCW1 (TQh, WIN, TQg);
  D_Flip_Flop FLO3 (.D(TQ1e), .clk(CLK), .Q(F3), .reset(RST));  // open: Qn, preset
  xor FWNX (TQ8, WIN, TQ7);
  and FLA0 (TQt, TQ19, TQs);
  and FCN1 (TQl, TQi, TQx);
  D_Flip_Flop FWND (.D(WIN), .clk(CLK), .Q(TQr), .reset(RST));  // open: Qn, preset
  D_Flip_Flop FCC2 (.D(TQk), .clk(CLK), .Q(TQ12), .reset(RST));  // open: Qn, preset
  and FLB0 (TQu, TQ1b, F0);
  and FLA3 (TQ1c, TQ19, TQ1a);
  and FLB3 (TQ1d, TQ1b, F3);
  D_Flip_Flop FSP (.D(SIG), .clk(CLK), .Q(TQ9), .reset(RST));  // open: Qn, preset

  // Other names for the same wires on the sheet: TQ1f = F3; TQ11 = F1; TQ16 = F2; TQ17 = CLK; TQ18 = RST; TQa = SIG;
  //   TQp = WIN; TQw = F0
endmodule
