// Logisim project full_adder.circ as structural Verilog
module full_adder (
  input  A,
  input  B,
  input  Cin,
  output SUM,
  output Cout
);

  wire and_2_out;

  xor xor_1 (A, A, A);
  and and_1 (A, A, A);
  xor xor_2 (Cout, A, Cin);
  and and_2 (and_2_out, A, Cin);
  or or_1 (Cout, A, and_2_out);

  assign B = A;
  assign SUM = Cout;
endmodule
