// Logisim project graycnt_2bit_test.circ as structural Verilog
module graycnt_2bit_test (
  input  RST,
  output G0,
  output Q0,
  output G1,
  output Q1
);

  wire CLK_out, N1_out, X2_out;

  Clock CLK (.out(CLK_out));
  D_Flip_Flop U1 (.D(N1_out), .clk(CLK_out), .Q(Q0), .preset(RST), .reset(RST));  // open: Qn
  D_Flip_Flop U2 (.D(X2_out), .clk(CLK_out), .Q(G1), .preset(RST), .reset(RST));  // open: Qn
  not N1 (N1_out, Q0);
  xor X2 (X2_out, G1, Q0);
  xor G3 (G0, Q0, G1);

  assign Q1 = G1;
endmodule
