// Logisim project graycnt_4bit_test.circ as structural Verilog
module graycnt_4bit_test (
  input  RST,
  output G0,
  output Q0,
  output G1,
  output Q1,
  output G2,
  output Q2,
  output G3,
  output Q3
);

  wire A3_out, A5_out, CLK_out, N1_out, X2_out, X4_out, X6_out;

  Clock CLK (.out(CLK_out));
  D_Flip_Flop U1 (.D(N1_out), .clk(CLK_out), .Q(Q0), .preset(RST), .reset(RST));  // open: Qn
  D_Flip_Flop U2 (.D(X2_out), .clk(CLK_out), .Q(Q1), .preset(RST), .reset(RST));  // open: Qn
  D_Flip_Flop U3 (.D(X4_out), .clk(CLK_out), .Q(Q2), .preset(RST), .reset(RST));  // open: Qn
  D_Flip_Flop U4 (.D(X6_out), .clk(CLK_out), .Q(G3), .preset(RST), .reset(RST));  // open: Qn
  not N1 (N1_out, Q0);
  xor X2 (X2_out, Q1, Q0);
  and A3 (A3_out, Q0, Q1);
  xor X4 (X4_out, Q2, A3_out);
  and A5 (A5_out, A3_out, Q2);
  xor X6 (X6_out, G3, A5_out);
  xor G7 (G0, Q0, Q1);
  xor G8 (G1, Q1, Q2);
  xor G9 (G2, Q2, G3);

  assign Q3 = G3;
endmodule
