// Logisim project hex7seg.circ as structural Verilog
module hex7seg (
  input  B0,
  input  B1,
  input  B2,
  input  B3,
  output a,
  output b,
  output c,
  output d,
  output e,
  output f,
  output g
);

  wire TQ0, TQ1, TQ1a, TQ1b, TQ1c, TQ1d, TQ1e, TQ1f, TQ1g, TQ1h, TQ1i, TQ1j, TQ1k, TQ1l, TQ1m, TQ1n, TQ1o,
       TQ1p, TQ1q, TQ1r, TQ1s, TQ1t, TQ1u, TQ1v, TQ1w, TQ1x, TQ1y, TQ1z, TQ2, TQ2a, TQ2b, TQ2c, TQ2d, TQ2e,
       TQ2f, TQ2g, TQ2h, TQ2i, TQ2j, TQ2k, TQ2l, TQ2m, TQ2n, TQ2o, TQ2p, TQ2r, TQ2s, TQ2t, TQ2u, TQ2v, TQ2w,
       TQ2x, TQ2y, TQ2z, TQ3, TQ3a, TQ3b, TQ3d, TQ3e, TQ3f, TQ3g, TQ3h, TQ3i, TQ3j, TQ3k, TQ3l, TQ3m, TQ3n,
       TQ3o, TQ3p, TQ3q, TQ3r, TQ3s, TQ3t, TQ3u, TQ3v, TQ3w, TQ3x, TQ3y, TQ3z, TQ4, TQ4a, TQ4b, TQ4c, TQ4d,
       TQ4e, TQ4f, TQ4g, TQ4h, TQ4i, TQ4j, TQ4k, TQ4l, TQ4m, TQ4n, TQ4o, TQ4p, TQ4q, TQ4r, TQ4s, TQ4t, TQ4u,
       TQ4v, TQ4w, TQ4x, TQ4y, TQ4z, TQ5, TQ5a, TQ5b, TQ5c, TQ5d, TQ5e, TQ5f, TQ5g, TQ5h, TQ5i, TQ5k, TQ5l,
       TQ5m, TQ5n, TQ5o, TQ5p, TQ5q, TQ5r, TQ5s, TQ5t, TQ5u, TQ5v, TQ5w, TQ5x, TQ5y, TQ5z, TQ6, TQ6a, TQ6b,
       TQ6c, TQ6d, TQ6e, TQ6f, TQ6g, TQ6h, TQ6i, TQ6j, TQ6k, TQ6l, TQ6m, TQ6n, TQ6o, TQ6p, TQ6q, TQ6r, TQ6s,
       TQ6t, TQ6v, TQ6w, TQ6x, TQ6y, TQ6z, TQ7, TQ7a, TQ7b, TQ7c, TQ7d, TQ7e, TQ7f, TQ7g, TQ7h, TQ7i, TQ7j,
       TQ7k, TQ7l, TQ7m, TQ7n, TQ7o, TQ7p, TQ7q, TQ7r, TQ7s, TQ7t, TQ7u, TQ7v, TQ7w, TQ7y, TQ7z, TQ8, TQ8a,
       TQ8b, TQ8c, TQ8d, TQ8e, TQ8f, TQ8g, TQ8h, TQ8i, TQ8j, TQ8k, TQ8l, TQ8m, TQ8n, TQ8o, TQ8p, TQ8q, TQ8r,
       TQ8s, TQ9, TQ10, TQ11, TQ12, TQ13, TQ14, TQ15, TQ16, TQ17, TQ18, TQ19, TQ20, TQ21, TQ22, TQ23, TQ24,
       TQ25, TQ26, TQ27, TQ28, TQ29, TQ31, TQ33, TQ34, TQ36, TQ37, TQ39, TQ40, TQ41, TQ42, TQ43, TQ44, TQ45,
       TQ46, TQ47, TQ49, TQ50, TQ51, TQ52, TQ53, TQ54, TQ55, TQ56, TQ57, TQ58, TQ59, TQ60, TQ61, TQ62, TQ63,
       TQ64, TQ65, TQ66, TQ67, TQ68, TQ69, TQ70, TQ71, TQ72, TQ73, TQ74, TQ75, TQ76, TQ77, TQ78, TQ79, TQ80,
       TQ81, TQ82, TQ83, TQ84, TQ85, TQ86, TQ87, TQ88, TQ89, TQa, TQb, TQc, TQd, TQe, TQf, TQg, TQh, TQj,
       TQk, TQl, TQm, TQn, TQo, TQp, TQq, TQr, TQs, TQt, TQu, TQv, TQw, TQx, TQy, TQz;

  not B7N1 (TQ2s, B0);
  and B7P9 (TQj, TQh, TQ2c);
  and B7P21 (TQ16, TQ14, B2);
  and B7P33 (TQ1v, TQ1t, TQ2c);
  and B7P45 (TQ2l, TQ2i, B2);
  and B7P57 (TQ3f, TQ3d, TQ1i);
  and B7P69 (TQ3r, TQ3p, TQ1i);
  and B7P81 (TQ43, TQ41, B3);
  or B7O93 (TQ4h, TQ4d, TQ4e);
  or B7O105 (TQ4t, TQ4p, TQ4q);
  or B7O117 (TQ55, TQ51, TQ52);
  or B7O129 (TQ5h, TQ5d, TQ5e);
  and B7P141 (TQ5q, B0, B1);
  and B7P153 (TQ62, TQ2s, TQ2j);
  and B7P165 (TQ6e, B0, B1);
  and B7P177 (TQ6q, TQ2s, B1);
  and B7P189 (TQ72, TQ71, B2);
  and B7P201 (TQ7e, TQ7d, TQ2c);
  and B7P213 (TQ7q, TQ7p, B2);
  and B7P225 (TQ83, TQ81, TQ1i);
  and B7P237 (TQ8f, TQ8d, B3);
  and B7P249 (TQ8r, TQ8p, B3);
  and B7P261 (TQg, TQd, B3);
  or B7O273 (TQ1a, TQ12, TQ13);
  or B7O285 (TQ1z, TQ1r, TQ1s);
  or B7O297 (TQ2p, TQ2g, TQ2h);
  or B7O309 (g, TQ39, TQ3a);
  not B7N2 (TQ2j, B1);
  and B7P10 (TQm, TQj, TQ1i);
  and B7P22 (TQ19, TQ16, TQ1i);
  and B7P34 (TQ1y, TQ1v, B3);
  and B7P46 (TQ2o, TQ2l, B3);
  or B7O58 (TQ3i, TQ3e, TQ3f);
  or B7O70 (TQ3u, TQ3q, TQ3r);
  or B7O82 (TQ46, TQ42, TQ43);
  and B7P94 (TQ4f, B0, B1);
  and B7P106 (TQ4r, TQ2s, B1);
  and B7P118 (TQ53, B0, TQ2j);
  and B7P130 (TQ5f, B0, TQ2j);
  and B7P142 (TQ5r, TQ5q, TQ2c);
  and B7P154 (TQ63, TQ62, TQ2c);
  and B7P166 (TQ6f, TQ6e, TQ2c);
  and B7P178 (TQ6r, TQ6q, B2);
  and B7P190 (TQ74, TQ72, TQ1i);
  and B7P202 (TQ7g, TQ7e, B3);
  and B7P214 (TQ7s, TQ7q, B3);
  or B7O226 (TQ86, TQ82, TQ83);
  or B7O238 (TQ8i, TQ8e, TQ8f);
  or B7O250 (TQ1, TQ8q, TQ8r);
  or B7O262 (f, TQf, TQg);
  and B7P274 (TQ15, B0, TQ2j);
  and B7P286 (TQ1u, B0, TQ2j);
  and B7P298 (TQ2k, B0, TQ2j);
  not B7N3 (TQ2c, B2);
  not B7N4 (TQ1i, B3);
  or B7O11 (TQs, TQl, TQm);
  or B7O23 (TQ1g, TQ18, TQ19);
  or B7O35 (TQ25, TQ1x, TQ1y);
  or B7O47 (a, TQ2n, TQ2o);
  and B7P59 (TQ3g, B0, B1);
  and B7P71 (TQ3s, TQ2s, TQ2j);
  and B7P83 (TQ44, B0, TQ2j);
  and B7P95 (TQ4g, TQ4f, TQ2c);
  and B7P107 (TQ4s, TQ4r, B2);
  and B7P119 (TQ54, TQ53, TQ2c);
  and B7P131 (TQ5g, TQ5f, B2);
  and B7P143 (TQ5t, TQ5r, TQ1i);
  and B7P155 (TQ65, TQ63, B3);
  and B7P167 (TQ6h, TQ6f, B3);
  and B7P179 (TQ6t, TQ6r, B3);
  or B7O191 (TQ77, TQ73, TQ74);
  or B7O203 (TQ7j, TQ7f, TQ7g);
  or B7O215 (TQ7v, TQ7r, TQ7s);
  and B7P227 (TQ84, B0, TQ2j);
  and B7P239 (TQ8g, B0, TQ2j);
  and B7P251 (TQ8s, TQ2s, TQ2j);
  and B7P263 (TQk, TQ2s, B1);
  and B7P275 (TQ17, TQ15, B2);
  and B7P287 (TQ1w, TQ1u, TQ2c);
  and B7P299 (TQ2m, TQ2k, B2);
  and B7P1 (TQ3, TQ2s, TQ2j);
  and B7P12 (TQo, B0, TQ2j);
  and B7P24 (TQ1c, TQ2s, TQ2j);
  and B7P36 (TQ21, TQ2s, TQ2j);
  and B7P48 (TQ2t, TQ2s, TQ2j);
  and B7P60 (TQ3h, TQ3g, TQ2c);
  and B7P72 (TQ3t, TQ3s, TQ2c);
  and B7P84 (TQ45, TQ44, B2);
  and B7P96 (TQ4i, TQ4g, TQ1i);
  and B7P108 (TQ4u, TQ4s, TQ1i);
  and B7P120 (TQ56, TQ54, B3);
  and B7P132 (TQ5i, TQ5g, B3);
  or B7O144 (TQ5w, TQ5s, TQ5t);
  or B7O156 (TQ68, TQ64, TQ65);
  or B7O168 (TQ6k, TQ6g, TQ6h);
  or B7O180 (d, TQ6s, TQ6t);
  and B7P192 (TQ75, TQ2s, TQ2j);
  and B7P204 (TQ7h, TQ2s, TQ2j);
  and B7P216 (TQ7t, B0, B1);
  and B7P228 (TQ85, TQ84, B2);
  and B7P240 (TQ8h, TQ8g, TQ2c);
  and B7P252 (TQ0, TQ8s, B2);
  and B7P264 (TQn, TQk, TQ2c);
  and B7P276 (TQ1b, TQ17, TQ1i);
  and B7P288 (TQ20, TQ1w, B3);
  and B7P300 (TQ2r, TQ2m, B3);
  and B7P2 (TQ5, TQ3, TQ2c);
  and B7P13 (TQq, TQo, B2);
  and B7P25 (TQ1e, TQ1c, TQ2c);
  and B7P37 (TQ23, TQ21, B2);
  and B7P49 (TQ2v, TQ2t, TQ2c);
  and B7P61 (TQ3j, TQ3h, TQ1i);
  and B7P73 (TQ3v, TQ3t, B3);
  and B7P85 (TQ47, TQ45, B3);
  or B7O97 (TQ4l, TQ4h, TQ4i);
  or B7O109 (TQ4x, TQ4t, TQ4u);
  or B7O121 (TQ59, TQ55, TQ56);
  or B7O133 (c, TQ5h, TQ5i);
  and B7P145 (TQ5u, B0, TQ2j);
  and B7P157 (TQ66, B0, TQ2j);
  and B7P169 (TQ6i, TQ2s, TQ2j);
  and B7P181 (TQ6v, TQ2s, TQ2j);
  and B7P193 (TQ76, TQ75, TQ2c);
  and B7P205 (TQ7i, TQ7h, B2);
  and B7P217 (TQ7u, TQ7t, B2);
  and B7P229 (TQ87, TQ85, TQ1i);
  and B7P241 (TQ8j, TQ8h, B3);
  and B7P253 (TQ2, TQ0, B3);
  and B7P265 (TQu, TQn, TQ1i);
  or B7O277 (TQ1j, TQ1a, TQ1b);
  or B7O289 (TQ27, TQ1z, TQ20);
  or B7O301 (TQ2x, TQ2p, TQ2r);
  and B7P3 (TQc, TQ5, TQ1i);
  and B7P14 (TQt, TQq, TQ1i);
  and B7P26 (TQ1h, TQ1e, B3);
  and B7P38 (TQ26, TQ23, B3);
  and B7P50 (TQ34, TQ2v, TQ1i);
  or B7O62 (TQ3m, TQ3i, TQ3j);
  or B7O74 (TQ3y, TQ3u, TQ3v);
  or B7O86 (b, TQ46, TQ47);
  and B7P98 (TQ4j, TQ2s, TQ2j);
  and B7P110 (TQ4v, B0, B1);
  and B7P122 (TQ57, TQ2s, B1);
  and B7P134 (TQ5k, TQ2s, TQ2j);
  and B7P146 (TQ5v, TQ5u, B2);
  and B7P158 (TQ67, TQ66, TQ2c);
  and B7P170 (TQ6j, TQ6i, B2);
  and B7P182 (TQ6w, TQ6v, TQ2c);
  and B7P194 (TQ78, TQ76, B3);
  and B7P206 (TQ7k, TQ7i, B3);
  and B7P218 (TQ7w, TQ7u, B3);
  or B7O230 (TQ8a, TQ86, TQ87);
  or B7O242 (TQ8m, TQ8i, TQ8j);
  or B7O254 (TQ7, TQ1, TQ2);
  and B7P266 (TQp, B0, B1);
  and B7P278 (TQ1d, TQ2s, B1);
  and B7P290 (TQ22, TQ2s, B1);
  and B7P302 (TQ2u, TQ2s, B1);
  and B7P4 (TQ9, TQ2s, B1);
  or B7O15 (TQ10, TQs, TQt);
  or B7O27 (TQ1p, TQ1g, TQ1h);
  or B7O39 (TQ2e, TQ25, TQ26);
  and B7P51 (TQ2z, B0, TQ2j);
  and B7P63 (TQ3k, TQ2s, TQ2j);
  and B7P75 (TQ3w, B0, TQ2j);
  and B7P87 (TQ49, TQ2s, TQ2j);
  and B7P99 (TQ4k, TQ4j, B2);
  and B7P111 (TQ4w, TQ4v, B2);
  and B7P123 (TQ58, TQ57, TQ2c);
  and B7P135 (TQ5l, TQ5k, TQ2c);
  and B7P147 (TQ5x, TQ5v, TQ1i);
  and B7P159 (TQ69, TQ67, B3);
  and B7P171 (TQ6l, TQ6j, B3);
  and B7P183 (TQ6z, TQ6w, TQ1i);
  or B7O195 (TQ7b, TQ77, TQ78);
  or B7O207 (TQ7n, TQ7j, TQ7k);
  or B7O219 (e, TQ7v, TQ7w);
  and B7P231 (TQ88, TQ2s, B1);
  and B7P243 (TQ8k, TQ2s, B1);
  and B7P255 (TQ4, TQ2s, B1);
  and B7P267 (TQr, TQp, TQ2c);
  and B7P279 (TQ1f, TQ1d, B2);
  and B7P291 (TQ24, TQ22, TQ2c);
  and B7P303 (TQ2w, TQ2u, B2);
  and B7P5 (TQa, TQ9, TQ2c);
  and B7P16 (TQw, TQ2s, B1);
  and B7P28 (TQ1l, B0, TQ2j);
  and B7P40 (TQ29, TQ2s, B1);
  and B7P52 (TQ31, TQ2z, TQ2c);
  and B7P64 (TQ3l, TQ3k, B2);
  and B7P76 (TQ3x, TQ3w, TQ2c);
  and B7P88 (TQ4a, TQ49, TQ2c);
  and B7P100 (TQ4m, TQ4k, TQ1i);
  and B7P112 (TQ4y, TQ4w, TQ1i);
  and B7P124 (TQ5a, TQ58, B3);
  and B7P136 (TQ5o, TQ5l, TQ1i);
  or B7O148 (TQ60, TQ5w, TQ5x);
  or B7O160 (TQ6c, TQ68, TQ69);
  or B7O172 (TQ6o, TQ6k, TQ6l);
  and B7P184 (TQ6x, TQ2s, B1);
  and B7P196 (TQ79, TQ2s, B1);
  and B7P208 (TQ7l, B0, TQ2j);
  and B7P220 (TQ7y, TQ2s, TQ2j);
  and B7P232 (TQ89, TQ88, B2);
  and B7P244 (TQ8l, TQ8k, TQ2c);
  and B7P256 (TQ6, TQ4, B2);
  and B7P268 (TQv, TQr, TQ1i);
  and B7P280 (TQ1k, TQ1f, TQ1i);
  and B7P292 (TQ28, TQ24, B3);
  and B7P304 (TQ2y, TQ2w, B3);
  and B7P6 (TQe, TQa, TQ1i);
  and B7P17 (TQy, TQw, B2);
  and B7P29 (TQ1n, TQ1l, TQ2c);
  and B7P41 (TQ2b, TQ29, B2);
  and B7P53 (TQ37, TQ31, TQ1i);
  and B7P65 (TQ3n, TQ3l, TQ1i);
  and B7P77 (TQ3z, TQ3x, B3);
  and B7P89 (TQ4d, TQ4a, TQ1i);
  or B7O101 (TQ4p, TQ4l, TQ4m);
  or B7O113 (TQ51, TQ4x, TQ4y);
  or B7O125 (TQ5d, TQ59, TQ5a);
  and B7P137 (TQ5m, TQ2s, B1);
  and B7P149 (TQ5y, TQ2s, B1);
  and B7P161 (TQ6a, TQ2s, B1);
  and B7P173 (TQ6m, B0, TQ2j);
  and B7P185 (TQ6y, TQ6x, TQ2c);
  and B7P197 (TQ7a, TQ79, TQ2c);
  and B7P209 (TQ7m, TQ7l, B2);
  and B7P221 (TQ7z, TQ7y, TQ2c);
  and B7P233 (TQ8b, TQ89, TQ1i);
  and B7P245 (TQ8n, TQ8l, B3);
  and B7P257 (TQ8, TQ6, B3);
  or B7O269 (TQ12, TQu, TQv);
  or B7O281 (TQ1r, TQ1j, TQ1k);
  or B7O293 (TQ2g, TQ27, TQ28);
  or B7O305 (TQ39, TQ2x, TQ2y);
  or B7O7 (TQl, TQc, TQe);
  and B7P18 (TQ11, TQy, TQ1i);
  and B7P30 (TQ1q, TQ1n, B3);
  and B7P42 (TQ2f, TQ2b, B3);
  or B7O54 (TQ3e, TQ34, TQ37);
  or B7O66 (TQ3q, TQ3m, TQ3n);
  or B7O78 (TQ42, TQ3y, TQ3z);
  and B7P90 (TQ4b, B0, TQ2j);
  and B7P102 (TQ4n, B0, TQ2j);
  and B7P114 (TQ4z, TQ2s, TQ2j);
  and B7P126 (TQ5b, B0, B1);
  and B7P138 (TQ5n, TQ5m, TQ2c);
  and B7P150 (TQ5z, TQ5y, B2);
  and B7P162 (TQ6b, TQ6a, TQ2c);
  and B7P174 (TQ6n, TQ6m, B2);
  and B7P186 (TQ70, TQ6y, TQ1i);
  and B7P198 (TQ7c, TQ7a, B3);
  and B7P210 (TQ7o, TQ7m, B3);
  and B7P222 (TQ82, TQ7z, TQ1i);
  or B7O234 (TQ8e, TQ8a, TQ8b);
  or B7O246 (TQ8q, TQ8m, TQ8n);
  or B7O258 (TQf, TQ7, TQ8);
  and B7P270 (TQx, TQ2s, TQ2j);
  and B7P282 (TQ1m, TQ2s, TQ2j);
  and B7P294 (TQ2a, B0, B1);
  and B7P306 (TQ33, B0, B1);
  and B7P8 (TQh, B0, B1);
  or B7O19 (TQ18, TQ10, TQ11);
  or B7O31 (TQ1x, TQ1p, TQ1q);
  or B7O43 (TQ2n, TQ2e, TQ2f);
  and B7P55 (TQ3b, TQ2s, B1);
  and B7P67 (TQ3o, B0, B1);
  and B7P79 (TQ40, TQ2s, B1);
  and B7P91 (TQ4c, TQ4b, TQ2c);
  and B7P103 (TQ4o, TQ4n, B2);
  and B7P115 (TQ50, TQ4z, TQ2c);
  and B7P127 (TQ5c, TQ5b, TQ2c);
  and B7P139 (TQ5p, TQ5n, TQ1i);
  and B7P151 (TQ61, TQ5z, TQ1i);
  and B7P163 (TQ6d, TQ6b, B3);
  and B7P175 (TQ6p, TQ6n, B3);
  or B7O187 (TQ73, TQ6z, TQ70);
  or B7O199 (TQ7f, TQ7b, TQ7c);
  or B7O211 (TQ7r, TQ7n, TQ7o);
  and B7P223 (TQ80, TQ2s, TQ2j);
  and B7P235 (TQ8c, TQ2s, TQ2j);
  and B7P247 (TQ8o, B0, B1);
  and B7P259 (TQb, B0, B1);
  and B7P271 (TQz, TQx, B2);
  and B7P283 (TQ1o, TQ1m, TQ2c);
  and B7P295 (TQ2d, TQ2a, TQ2c);
  and B7P307 (TQ36, TQ33, B2);
  and B7P20 (TQ14, B0, B1);
  and B7P32 (TQ1t, TQ2s, B1);
  and B7P44 (TQ2i, B0, B1);
  and B7P56 (TQ3d, TQ3b, TQ2c);
  and B7P68 (TQ3p, TQ3o, B2);
  and B7P80 (TQ41, TQ40, TQ2c);
  and B7P92 (TQ4e, TQ4c, TQ1i);
  and B7P104 (TQ4q, TQ4o, TQ1i);
  and B7P116 (TQ52, TQ50, B3);
  and B7P128 (TQ5e, TQ5c, B3);
  or B7O140 (TQ5s, TQ5o, TQ5p);
  or B7O152 (TQ64, TQ60, TQ61);
  or B7O164 (TQ6g, TQ6c, TQ6d);
  or B7O176 (TQ6s, TQ6o, TQ6p);
  and B7P188 (TQ71, TQ2s, B1);
  and B7P200 (TQ7d, B0, B1);
  and B7P212 (TQ7p, TQ2s, B1);
  and B7P224 (TQ81, TQ80, B2);
  and B7P236 (TQ8d, TQ8c, TQ2c);
  and B7P248 (TQ8p, TQ8o, TQ2c);
  and B7P260 (TQd, TQb, B2);
  and B7P272 (TQ13, TQz, TQ1i);
  and B7P284 (TQ1s, TQ1o, B3);
  and B7P296 (TQ2h, TQ2d, B3);
  and B7P308 (TQ3a, TQ36, B3);

  // Other names for the same wires on the sheet: TQ2q = a; TQ3c = g; TQ5j = c; TQ6u = d; TQ7x = e; TQ30 = B0;
  //   TQ32 = B1; TQ35 = B2; TQ38 = B3; TQ48 = b; TQi = f
endmodule
