// Logisim project jk_flipflop.circ as structural Verilog
module jk_flipflop (
  input  PRE,
  input  J,
  input  K,
  input  CLK,
  input  CLR,
  output Q,
  output nQ
);

  J_K_Flip_Flop JK (.J(J), .K(K), .clk(CLK), .Q(Q), .Qn(nQ), .preset(CLR), .reset(PRE));
endmodule
