// Logisim project mac_4bit.circ as structural Verilog
module mac_4bit (
  input  CLK,
  input  RST,
  input  GND,
  input  A0,
  input  A1,
  input  A2,
  input  A3,
  input  B0,
  input  B1,
  input  B2,
  input  B3,
  output Q0,
  output Q1,
  output Q2,
  output Q3,
  output Q4,
  output Q5,
  output Q6,
  output Q7
);

  wire TQ0, TQ1, TQ1a, TQ1b, TQ1c, TQ1d, TQ1e, TQ1f, TQ1g, TQ1h, TQ1i, TQ1j, TQ1k, TQ1l, TQ1m, TQ1n, TQ1o,
       TQ1p, TQ1q, TQ1r, TQ1s, TQ1t, TQ1u, TQ1v, TQ1w, TQ1x, TQ1y, TQ1z, TQ2, TQ2a, TQ2b, TQ2c, TQ2d, TQ2f,
       TQ2h, TQ2i, TQ2j, TQ2l, TQ2m, TQ2n, TQ2o, TQ2p, TQ2r, TQ2t, TQ2u, TQ2v, TQ2w, TQ2y, TQ2z, TQ3a, TQ3b,
       TQ3c, TQ3d, TQ3e, TQ3f, TQ3g, TQ3h, TQ3i, TQ3j, TQ3k, TQ3l, TQ3m, TQ3n, TQ3o, TQ3p, TQ3q, TQ3r, TQ3s,
       TQ3t, TQ3u, TQ3v, TQ3w, TQ3x, TQ3y, TQ3z, TQ4, TQ4a, TQ4b, TQ4c, TQ4d, TQ4e, TQ4f, TQ4g, TQ4h, TQ4i,
       TQ4j, TQ4k, TQ4l, TQ4m, TQ4n, TQ4o, TQ4p, TQ4q, TQ4r, TQ4s, TQ4t, TQ4u, TQ4v, TQ4w, TQ4x, TQ4y, TQ4z,
       TQ5, TQ6, TQ7, TQ8, TQ9, TQ10, TQ11, TQ12, TQ13, TQ14, TQ15, TQ16, TQ17, TQ18, TQ19, TQ20, TQ21, TQ22,
       TQ23, TQ24, TQ25, TQ26, TQ27, TQ28, TQ30, TQ31, TQ32, TQ34, TQ38, TQ39, TQ40, TQ41, TQ42, TQ43, TQ44,
       TQ45, TQ46, TQ47, TQ48, TQ49, TQ50, TQ51, TQ52, TQ53, TQ54, TQb, TQc, TQd, TQf, TQh, TQi, TQn, TQo,
       TQp, TQq, TQr, TQs, TQt, TQu, TQv, TQw, TQx, TQy, TQz;

  D_Flip_Flop U1 (.D(TQ2a), .clk(CLK), .Q(Q0), .reset(RST));  // open: Qn, preset
  and MACP5 (TQt, A0, B1);
  xor MACX17 (TQv, TQr, TQt);
  xor MACX19 (TQ1l, TQ1g, TQ1i);
  xor MACX21 (TQ28, GND, GND);
  xor MACX23 (TQ2y, TQ2u, TQ2v);
  xor MACX25 (TQ3i, TQ3f, TQ3g);
  xor MACX27 (TQ3s, GND, GND);
  xor MACX29 (TQ45, TQ42, TQ43);
  xor MACX31 (TQ4j, TQ4g, TQ4h);
  xor MACX33 (TQ4u, GND, GND);
  xor MACY35 (TQ54, TQ53, Q0);
  xor MACY37 (TQd, TQb, Q2);
  xor MACY39 (TQ11, TQz, Q4);
  xor MACY41 (TQ1r, TQ1p, Q6);
  and MACP6 (TQ15, A1, B1);
  xor MACS17 (TQ4, TQv, GND);
  xor MACS19 (TQ2u, TQ1l, TQ1k);
  xor MACS21 (TQ3f, TQ28, TQ27);
  xor MACS23 (TQ3w, TQ2y, TQ2w);
  xor MACS25 (TQ49, TQ3i, TQ3h);
  xor MACS27 (TQ4n, TQ3s, TQ3r);
  xor MACS29 (TQz, TQ45, TQ44);
  xor MACS31 (TQ1p, TQ4j, TQ4i);
  // XOR_Gate MACS33 has open pins: in0=TQ4u, in1=TQ4t, out=open
  xor MACT35 (TQ2a, TQ54, GND);
  xor MACT37 (TQ2h, TQd, TQc);
  xor MACT39 (TQ2r, TQ11, TQ10);
  xor MACT41 (TQ2z, TQ1r, TQ1q);
  D_Flip_Flop U2 (.D(TQ2f), .clk(CLK), .Q(Q1), .reset(RST));  // open: Qn, preset
  and MACP7 (TQ1i, A2, B1);
  and MACA17 (TQw, TQr, TQt);
  and MACA19 (TQ1m, TQ1g, TQ1i);
  and MACA21 (TQ2b, GND, GND);
  and MACA23 (TQ30, TQ2u, TQ2v);
  and MACA25 (TQ3j, TQ3f, TQ3g);
  and MACA27 (TQ3t, GND, GND);
  and MACA29 (TQ46, TQ42, TQ43);
  and MACA31 (TQ4k, TQ4g, TQ4h);
  and MACA33 (TQ4v, GND, GND);
  and MACH35 (TQ0, TQ53, Q0);
  and MACH37 (TQf, TQb, Q2);
  and MACH39 (TQ12, TQz, Q4);
  and MACH41 (TQ1s, TQ1p, Q6);
  D_Flip_Flop U3 (.D(TQ2h), .clk(CLK), .Q(Q2), .reset(RST));  // open: Qn, preset
  and MACP8 (TQ1u, A3, B1);
  and MACB17 (TQx, GND, TQv);
  and MACB19 (TQ1n, TQ1k, TQ1l);
  and MACB21 (TQ2c, TQ27, TQ28);
  and MACB23 (TQ31, TQ2w, TQ2y);
  and MACB25 (TQ3k, TQ3h, TQ3i);
  and MACB27 (TQ3u, TQ3r, TQ3s);
  and MACB29 (TQ47, TQ44, TQ45);
  and MACB31 (TQ4l, TQ4i, TQ4j);
  and MACB33 (TQ4w, TQ4t, TQ4u);
  and MACI35 (TQ1, GND, TQ54);
  and MACI37 (TQh, TQc, TQd);
  and MACI39 (TQ14, TQ10, TQ11);
  and MACI41 (TQ1t, TQ1q, TQ1r);
  D_Flip_Flop U4 (.D(TQ2m), .clk(CLK), .Q(Q3), .reset(RST));  // open: Qn, preset
  and MACP9 (TQ2j, A0, B2);
  or MACO17 (TQy, TQw, TQx);
  or MACO19 (TQ1o, TQ1m, TQ1n);
  or MACO21 (TQ2d, TQ2b, TQ2c);
  or MACO23 (TQ32, TQ30, TQ31);
  or MACO25 (TQ3l, TQ3j, TQ3k);
  or MACO27 (TQ3v, TQ3t, TQ3u);
  or MACO29 (TQ48, TQ46, TQ47);
  or MACO31 (TQ4m, TQ4k, TQ4l);
  or MACO33 (TQ4x, TQ4v, TQ4w);
  or MACJ35 (TQ2, TQ0, TQ1);
  or MACJ37 (TQi, TQf, TQh);
  or MACJ39 (TQ16, TQ12, TQ14);
  or MACJ41 (TQ1v, TQ1s, TQ1t);
  and MACP10 (TQ2v, A1, B2);
  or MACG17 (TQ17, TQy, GND);
  or MACG19 (TQ1w, TQ1o, GND);
  // OR_Gate MACG21 has open pins: in0=TQ2d, in1=GND, out=open
  or MACG23 (TQ3a, TQ32, GND);
  or MACG25 (TQ3m, TQ3l, GND);
  // OR_Gate MACG27 has open pins: in0=TQ3v, in1=GND, out=open
  or MACG29 (TQ4b, TQ48, GND);
  or MACG31 (TQ4o, TQ4m, GND);
  or MACG33 (TQ4y, TQ4x, GND);
  or MACK35 (TQ5, TQ2, GND);
  or MACK37 (TQo, TQi, GND);
  or MACK39 (TQ1d, TQ16, GND);
  or MACK41 (TQ22, TQ1v, GND);
  D_Flip_Flop U5 (.D(TQ2r), .clk(CLK), .Q(Q4), .reset(RST));  // open: Qn, preset
  and MACP11 (TQ39, A2, B2);
  xor MACX18 (TQ18, TQ13, TQ15);
  xor MACX20 (TQ1x, GND, TQ1u);
  xor MACX22 (TQ2l, TQ2i, TQ2j);
  xor MACX24 (TQ3b, TQ38, TQ39);
  xor MACX26 (TQ3n, GND, GND);
  xor MACX28 (TQ3y, TQ3w, TQ3x);
  xor MACX30 (TQ4c, TQ49, TQ4a);
  xor MACX32 (TQ4p, TQ4n, GND);
  xor MACX34 (TQ4z, GND, GND);
  xor MACY36 (TQ6, TQ4, Q1);
  xor MACY38 (TQp, TQn, Q3);
  xor MACY40 (TQ1e, TQ1c, Q5);
  xor MACY42 (TQ23, TQ21, Q7);
  D_Flip_Flop U6 (.D(TQ2t), .clk(CLK), .Q(Q5), .reset(RST));  // open: Qn, preset
  and MACP12 (TQ3g, A3, B2);
  xor MACS18 (TQ2i, TQ18, TQ17);
  xor MACS20 (TQ38, TQ1x, TQ1w);
  xor MACS22 (TQb, TQ2l, GND);
  xor MACS24 (TQ42, TQ3b, TQ3a);
  xor MACS26 (TQ4g, TQ3n, TQ3m);
  xor MACS28 (TQn, TQ3y, GND);
  xor MACS30 (TQ1c, TQ4c, TQ4b);
  xor MACS32 (TQ21, TQ4p, TQ4o);
  // XOR_Gate MACS34 has open pins: in0=TQ4z, in1=TQ4y, out=open
  xor MACT36 (TQ2f, TQ6, TQ5);
  xor MACT38 (TQ2m, TQp, TQo);
  xor MACT40 (TQ2t, TQ1e, TQ1d);
  xor MACT42 (TQ34, TQ23, TQ22);
  D_Flip_Flop U7 (.D(TQ2z), .clk(CLK), .Q(Q6), .reset(RST));  // open: Qn, preset
  and MACP13 (TQ3x, A0, B3);
  and MACA18 (TQ19, TQ13, TQ15);
  and MACA20 (TQ1y, GND, TQ1u);
  and MACA22 (TQ2n, TQ2i, TQ2j);
  and MACA24 (TQ3c, TQ38, TQ39);
  and MACA26 (TQ3o, GND, GND);
  and MACA28 (TQ3z, TQ3w, TQ3x);
  and MACA30 (TQ4d, TQ49, TQ4a);
  and MACA32 (TQ4q, TQ4n, GND);
  and MACA34 (TQ50, GND, GND);
  and MACH36 (TQ7, TQ4, Q1);
  and MACH38 (TQq, TQn, Q3);
  and MACH40 (TQ1f, TQ1c, Q5);
  and MACH42 (TQ24, TQ21, Q7);
  and MACP14 (TQ43, A1, B3);
  and MACB18 (TQ1a, TQ17, TQ18);
  and MACB20 (TQ1z, TQ1w, TQ1x);
  and MACB22 (TQ2o, GND, TQ2l);
  and MACB24 (TQ3d, TQ3a, TQ3b);
  and MACB26 (TQ3p, TQ3m, TQ3n);
  and MACB28 (TQ40, GND, TQ3y);
  and MACB30 (TQ4e, TQ4b, TQ4c);
  and MACB32 (TQ4r, TQ4o, TQ4p);
  and MACB34 (TQ51, TQ4y, TQ4z);
  and MACI36 (TQ8, TQ5, TQ6);
  and MACI38 (TQs, TQo, TQp);
  and MACI40 (TQ1h, TQ1d, TQ1e);
  and MACI42 (TQ25, TQ22, TQ23);
  D_Flip_Flop U8 (.D(TQ34), .clk(CLK), .Q(Q7), .reset(RST));  // open: Qn, preset
  and MACP15 (TQ4a, A2, B3);
  or MACO18 (TQ1b, TQ19, TQ1a);
  or MACO20 (TQ20, TQ1y, TQ1z);
  or MACO22 (TQ2p, TQ2n, TQ2o);
  or MACO24 (TQ3e, TQ3c, TQ3d);
  or MACO26 (TQ3q, TQ3o, TQ3p);
  or MACO28 (TQ41, TQ3z, TQ40);
  or MACO30 (TQ4f, TQ4d, TQ4e);
  or MACO32 (TQ4s, TQ4q, TQ4r);
  or MACO34 (TQ52, TQ50, TQ51);
  or MACJ36 (TQ9, TQ7, TQ8);
  or MACJ38 (TQu, TQq, TQs);
  or MACJ40 (TQ1j, TQ1f, TQ1h);
  or MACJ42 (TQ26, TQ24, TQ25);
  and MACP16 (TQ4h, A3, B3);
  or MACG18 (TQ1k, TQ1b, GND);
  or MACG20 (TQ27, TQ20, GND);
  or MACG22 (TQ2w, TQ2p, GND);
  or MACG24 (TQ3h, TQ3e, GND);
  or MACG26 (TQ3r, TQ3q, GND);
  or MACG28 (TQ44, TQ41, GND);
  or MACG30 (TQ4i, TQ4f, GND);
  or MACG32 (TQ4t, TQ4s, GND);
  // OR_Gate MACG34 has open pins: in0=TQ52, in1=GND, out=open
  or MACK36 (TQc, TQ9, GND);
  or MACK38 (TQ10, TQu, GND);
  or MACK40 (TQ1q, TQ1j, GND);
  // OR_Gate MACK42 has open pins: in0=TQ26, in1=GND, out=open
  and MACP1 (TQ53, A0, B0);
  and MACP2 (TQr, A1, B0);
  and MACP3 (TQ13, A2, B0);
  and MACP4 (TQ1g, A3, B0);

  // Other names for the same wires on the sheet: TQ2e = Q0; TQ2g = Q1; TQ2k = Q2; TQ2q = Q3; TQ2s = Q4; TQ2x = Q5;
  //   TQ3 = B0; TQ29 = GND; TQ33 = Q6; TQ35 = CLK; TQ36 = RST; TQ37 = Q7; TQa = B1; TQe = B2; TQg = A0; TQj = A1;
  //   TQk = A2; TQl = A3; TQm = B3
endmodule
