// Logisim project mod10_counter.circ as structural Verilog
module mod10_counter (
  input  CLK,
  input  RST,
  output Q0,
  output Q1,
  output Q2,
  output Q3,
  output TC
);

  wire TQ1, TQ2, TQ5, TQ7, TQ9, TQa, TQb, TQc, TQd, TQe, TQf, TQh;

  T_Flip_Flop U1 (.T(TQ9), .clk(CLK), .Q(Q0), .reset(RST));  // open: Qn, preset
  and NR2 (TQc, Q0, Q1);
  and TM2 (TQb, TQc, TQe);
  T_Flip_Flop U2 (.T(TQa), .clk(CLK), .Q(Q1), .reset(RST));  // open: Qn, preset
  and NR3 (TQd, TQc, Q2);
  T_Flip_Flop U3 (.T(TQb), .clk(CLK), .Q(Q2), .reset(RST));  // open: Qn, preset
  and TM3 (TQf, TQd, TQe);
  T_Flip_Flop U4 (.T(TQh), .clk(CLK), .Q(Q3), .reset(RST));  // open: Qn, preset
  or TO3 (TQh, TQf, TC);
  not N2 (TQ1, Q1);
  and AT2 (TQ2, Q0, TQ1);
  not N3 (TQ5, Q2);
  and AT3 (TQ7, TQ2, TQ5);
  and AT4 (TC, TQ7, Q3);
  not NA (TQe, TC);
  or T0 (TQ9, TQe, TC);
  and TM1 (TQa, Q0, TQe);

  // Other names for the same wires on the sheet: TQ0 = Q1; TQ3 = Q2; TQ4 = CLK; TQ6 = RST; TQ8 = Q3; TQg = TC;
  //   TQi = Q0
endmodule
