// Logisim project mod6_counter.circ as structural Verilog
module mod6_counter (
  input  CLK,
  input  RST,
  output Q0,
  output Q1,
  output Q2,
  output Q3,
  output TC
);

  wire TQ1, TQ2, TQ6, TQ7, TQ9, TQa, TQb, TQd, TQe, TQf, TQg, TQh;

  T_Flip_Flop U1 (.T(TQ9), .clk(CLK), .Q(Q0), .reset(RST));  // open: Qn, preset
  and NR2 (TQe, Q0, Q1);
  and TM2 (TQb, TQe, TQg);
  T_Flip_Flop U2 (.T(TQa), .clk(CLK), .Q(Q1), .reset(RST));  // open: Qn, preset
  or TO2 (TQd, TQb, TC);
  T_Flip_Flop U3 (.T(TQd), .clk(CLK), .Q(Q2), .reset(RST));  // open: Qn, preset
  and NR3 (TQf, TQe, Q2);
  T_Flip_Flop U4 (.T(TQh), .clk(CLK), .Q(Q3), .reset(RST));  // open: Qn, preset
  and TM3 (TQh, TQf, TQg);
  not N2 (TQ1, Q1);
  and AT2 (TQ2, Q0, TQ1);
  and AT3 (TQ6, TQ2, Q2);
  not N4 (TQ7, Q3);
  and AT4 (TC, TQ6, TQ7);
  not NA (TQg, TC);
  or T0 (TQ9, TQg, TC);
  and TM1 (TQa, Q0, TQg);

  // Other names for the same wires on the sheet: TQ0 = Q1; TQ3 = Q2; TQ4 = CLK; TQ5 = RST; TQ8 = Q3; TQc = TC;
  //   TQi = Q0
endmodule
