// Logisim project mux_8to1.circ as structural Verilog
module mux_8to1 (
  input  D0,
  input  D1,
  input  D2,
  input  D3,
  input  D4,
  input  D5,
  input  D6,
  input  D7,
  input  S0,
  input  S1,
  input  S2,
  output Y
);

  wire TQ0, TQ2, TQ3, TQ4, TQ5, TQ6, TQ7, TQ8, TQ9, TQ11, TQ13, TQ14, TQ15, TQ16, TQ17, TQ18, TQa, TQb, TQc,
       TQd, TQe, TQf, TQg, TQh, TQi, TQj, TQk, TQp, TQr, TQt, TQv, TQx, TQz;

  and MUX0D (TQp, D0, TQ3);
  and MUX4D (TQx, D4, TQc);
  or MUXO1 (TQ14, TQp, TQr);
  and MUX0S1 (TQ2, TQg, TQd);
  and MUX4S1 (TQb, TQg, TQd);
  or MUXO2 (TQ15, TQ14, TQt);
  and MUX0S2 (TQ3, TQ2, TQ9);
  and MUX4S2 (TQc, TQb, S2);
  or MUXO3 (TQ16, TQ15, TQv);
  and MUX1D (TQr, D1, TQ5);
  and MUX5D (TQz, D5, TQf);
  or MUXO4 (TQ17, TQ16, TQx);
  and MUX1S1 (TQ4, S0, TQd);
  and MUX5S1 (TQe, S0, TQd);
  or MUXO5 (TQ18, TQ17, TQz);
  and MUX1S2 (TQ5, TQ4, TQ9);
  and MUX5S2 (TQf, TQe, S2);
  or MUXO6 (TQ0, TQ18, TQ11);
  and MUX2D (TQt, D2, TQ7);
  and MUX6D (TQ11, D6, TQi);
  or MUXO7 (Y, TQ0, TQ13);
  and MUX2S1 (TQ6, TQg, S1);
  and MUX6S1 (TQh, TQg, S1);
  not MUXN1 (TQg, S0);
  not MUXN2 (TQd, S1);
  and MUX2S2 (TQ7, TQ6, TQ9);
  and MUX6S2 (TQi, TQh, S2);
  and MUX3D (TQv, D3, TQa);
  and MUX7D (TQ13, D7, TQk);
  not MUXN3 (TQ9, S2);
  and MUX3S1 (TQ8, S0, S1);
  and MUX7S1 (TQj, S0, S1);
  and MUX3S2 (TQa, TQ8, TQ9);
  and MUX7S2 (TQk, TQj, S2);

  // Other names for the same wires on the sheet: TQ1 = Y; TQ10 = D6; TQ12 = D7; TQl = S0; TQm = S1; TQn = S2;
  //   TQo = D0; TQq = D1; TQs = D2; TQu = D3; TQw = D4; TQy = D5
endmodule
