// Logisim project ring_counter.circ as structural Verilog
module ring_counter (
  input  CLK,
  input  SEED,
  input  RST,
  output Q0,
  output Q1,
  output Q2,
  output Q3
);

  wire O1_out;

  D_Flip_Flop U1 (.D(O1_out), .clk(CLK), .Q(Q0), .preset(RST), .reset(RST));  // open: Qn
  D_Flip_Flop U2 (.D(Q0), .clk(CLK), .Q(Q1), .preset(RST), .reset(RST));  // open: Qn
  D_Flip_Flop U3 (.D(Q1), .clk(CLK), .Q(Q2), .preset(RST), .reset(RST));  // open: Qn
  D_Flip_Flop U4 (.D(Q2), .clk(CLK), .Q(Q3), .preset(RST), .reset(RST));  // open: Qn
  or O1 (O1_out, SEED, Q3);
endmodule
