// Logisim project satadd_4bit.circ as structural Verilog
module satadd_4bit (
  input  A0,
  input  B0,
  input  A1,
  input  B1,
  input  A2,
  input  B2,
  input  A3,
  input  B3,
  input  GND,
  output S0,
  output S1,
  output S2,
  output S3
);

  wire TQ2, TQ3, TQ4, TQ5, TQ8, TQ9, TQa, TQb, TQc, TQf, TQg, TQh, TQi, TQj, TQm, TQn, TQo, TQp, TQq, TQs,
       TQu, TQw, TQy, TQz;

  xor SAX1 (TQ2, A0, B0);
  xor SAX3 (TQg, A2, B2);
  or SAU5 (S0, TQs, TQz);
  xor SAS1 (TQs, TQ2, GND);
  xor SAS3 (TQw, TQg, TQf);
  or SAU6 (S1, TQu, TQz);
  and SAA1 (TQ3, A0, B0);
  and SAA3 (TQh, A2, B2);
  or SAU7 (S2, TQw, TQz);
  and SAB1 (TQ4, GND, TQ2);
  and SAB3 (TQi, TQf, TQg);
  or SAU8 (S3, TQy, TQz);
  or SAO1 (TQ5, TQ3, TQ4);
  or SAO3 (TQj, TQh, TQi);
  or SAG1 (TQ8, TQ5, GND);
  or SAG3 (TQm, TQj, GND);
  xor SAX2 (TQ9, A1, B1);
  xor SAX4 (TQn, A3, B3);
  xor SAS2 (TQu, TQ9, TQ8);
  xor SAS4 (TQy, TQn, TQm);
  and SAA2 (TQa, A1, B1);
  and SAA4 (TQo, A3, B3);
  and SAB2 (TQb, TQ8, TQ9);
  and SAB4 (TQp, TQm, TQn);
  or SAO2 (TQc, TQa, TQb);
  or SAO4 (TQq, TQo, TQp);
  or SAG2 (TQf, TQc, GND);
  or SAG4 (TQz, TQq, GND);

  // Other names for the same wires on the sheet: TQ0 = A0; TQ1 = B0; TQ6 = A1; TQ7 = B1; TQ10 = S3; TQd = A2;
  //   TQe = B2; TQk = A3; TQl = B3; TQr = GND; TQt = S0; TQv = S1; TQx = S2
endmodule
