// Logisim project stopwatch.circ as structural Verilog
module stopwatch (
  input  CLK,
  input  RUN,
  input  RST,
  output Q0,
  output Q1,
  output Q2,
  output Q3,
  output Q4,
  output Q5,
  output Q6
);

  wire TQ1, TQ3, TQ4, TQ5, TQ9, TQb, TQc, TQd, TQe, TQf, TQg, TQh, TQi, TQj, TQl, TQm, TQn, TQo, TQp, TQq,
       TQr, TQs, TQt, TQu, TQv, TQw;

  // NOT_Gate SWRN has open pins: in=RUN, out=open
  and SWUA3 (TQl, TQ5, Q3);
  not SWTN1 (TQm, Q5);
  T_Flip_Flop SWUF0 (.T(TQb), .clk(CLK), .Q(Q0), .reset(RST));  // open: Qn, preset
  not SWNA (TQ9, TQl);
  and SWTA1 (TQn, Q4, TQm);
  and SWUC (TQg, TQ9, RUN);
  and SWTA2 (TQo, TQn, Q6);
  T_Flip_Flop SWUF1 (.T(TQc), .clk(CLK), .Q(Q1), .reset(RST));  // open: Qn, preset
  and SWUW (TQi, TQl, RUN);
  not SWNT (TQp, TQo);
  T_Flip_Flop SWUF2 (.T(TQd), .clk(CLK), .Q(Q2), .reset(RST));  // open: Qn, preset
  or SWT0 (TQb, TQg, TQi);
  and SWTW (TQv, TQq, TQo);
  T_Flip_Flop SWUF3 (.T(TQj), .clk(CLK), .Q(Q3), .reset(RST));  // open: Qn, preset
  and SWUM1 (TQc, Q0, TQg);
  and SWTC (TQt, TQq, TQp);
  and SWNR2 (TQe, Q0, Q1);
  and SWTM1 (TQr, Q4, TQt);
  T_Flip_Flop SWTF0 (.T(TQq), .clk(CLK), .Q(Q4), .reset(RST));  // open: Qn, preset
  and SWUM2 (TQd, TQe, TQg);
  and SWTNR2 (TQs, Q4, Q5);
  T_Flip_Flop SWTF1 (.T(TQr), .clk(CLK), .Q(Q5), .reset(RST));  // open: Qn, preset
  and SWNR3 (TQf, TQe, Q2);
  and SWTM2 (TQu, TQs, TQt);
  T_Flip_Flop SWTF2 (.T(TQw), .clk(CLK), .Q(Q6), .reset(RST));  // open: Qn, preset
  and SWUM3 (TQh, TQf, TQg);
  or SWTO2 (TQw, TQu, TQv);
  or SWUO3 (TQj, TQh, TQi);
  not SWUN1 (TQ1, Q1);
  and SWTE (TQq, RUN, TQl);
  and SWUA1 (TQ3, Q0, TQ1);
  not SWUN2 (TQ4, Q2);
  and SWUA2 (TQ5, TQ3, TQ4);

  // Other names for the same wires on the sheet: TQ0 = Q3; TQ2 = Q4; TQ6 = Q5; TQ7 = CLK; TQ8 = RST; TQa = Q6;
  //   TQk = RUN; TQx = Q0; TQy = Q1; TQz = Q2
endmodule
