// Logisim project subtractor_4bit.circ as structural Verilog
module subtractor_4bit (
  input  A0,
  input  B0,
  input  A1,
  input  B1,
  input  A2,
  input  B2,
  input  A3,
  input  B3,
  input  Bin,
  output D0,
  output D1,
  output D2,
  output D3,
  output Bout
);

  wire TQ8, TQa, TQb, TQd, TQe, TQf, TQh, TQi, TQj, TQk, TQl, TQm, TQo, TQp, TQq, TQr, TQs, TQt, TQv, TQw,
       TQx, TQy, TQz;

  xor SUB0X (TQ8, A0, B0);
  and SUB1B (TQl, B1, TQj);
  or SUB3O (TQw, B3, TQx);
  xor SUB0D (D0, TQ8, Bin);
  or SUB1C (TQq, TQk, TQl);
  and SUB3A (TQy, TQv, TQw);
  not SUB0N (TQa, A0);
  xor SUB2X (TQm, A2, B2);
  and SUB3B (TQz, B3, TQx);
  or SUB0O (TQb, B0, Bin);
  xor SUB2D (D2, TQm, TQq);
  or SUB3C (Bout, TQy, TQz);
  and SUB0A (TQd, TQa, TQb);
  not SUB2N (TQo, A2);
  and SUB0B (TQe, B0, Bin);
  or SUB2O (TQp, B2, TQq);
  or SUB0C (TQj, TQd, TQe);
  and SUB2A (TQr, TQo, TQp);
  xor SUB1X (TQf, A1, B1);
  and SUB2B (TQs, B2, TQq);
  xor SUB1D (D1, TQf, TQj);
  or SUB2C (TQx, TQr, TQs);
  not SUB1N (TQh, A1);
  xor SUB3X (TQt, A3, B3);
  or SUB1O (TQi, B1, TQj);
  xor SUB3D (D3, TQt, TQx);
  and SUB1A (TQk, TQh, TQi);
  not SUB3N (TQv, A3);

  // Other names for the same wires on the sheet: TQ0 = A0; TQ1 = B0; TQ2 = A1; TQ3 = B1; TQ4 = A2; TQ5 = B2; TQ6 = A3;
  //   TQ7 = B3; TQ9 = D0; TQ10 = Bout; TQc = Bin; TQg = D1; TQn = D2; TQu = D3
endmodule
