// Logisim project subtractor_8bit.circ as structural Verilog
module subtractor_8bit (
  input  A0,
  input  B0,
  input  A1,
  input  B1,
  input  A2,
  input  B2,
  input  A3,
  input  B3,
  input  A4,
  input  B4,
  input  A5,
  input  B5,
  input  A6,
  input  B6,
  input  A7,
  input  B7,
  input  Bin,
  output D0,
  output D1,
  output D2,
  output D3,
  output D4,
  output D5,
  output D6,
  output D7,
  output Bout
);

  wire TQ1a, TQ1b, TQ1c, TQ1d, TQ1e, TQ1f, TQ1h, TQ1i, TQ1j, TQ1k, TQ1l, TQ1m, TQ1o, TQ1p, TQ1q, TQ1r, TQ1s,
       TQ1t, TQ1v, TQ1w, TQ1x, TQ1y, TQ1z, TQ10, TQ11, TQ13, TQ14, TQ15, TQ16, TQ17, TQ18, TQg, TQi, TQj,
       TQl, TQm, TQn, TQp, TQq, TQr, TQs, TQt, TQu, TQw, TQx, TQy, TQz;

  xor SUB0X (TQg, A0, B0);
  and SUB1B (TQt, B1, TQr);
  or SUB3O (TQ14, B3, TQ15);
  xor SUB5D (D5, TQ1f, TQ1j);
  or SUB6C (TQ1x, TQ1r, TQ1s);
  xor SUB0D (D0, TQg, Bin);
  or SUB1C (TQy, TQs, TQt);
  and SUB3A (TQ16, TQ13, TQ14);
  not SUB5N (TQ1h, A5);
  xor SUB7X (TQ1t, A7, B7);
  or SUB5O (TQ1i, B5, TQ1j);
  not SUB0N (TQi, A0);
  xor SUB2X (TQu, A2, B2);
  and SUB3B (TQ17, B3, TQ15);
  xor SUB7D (D7, TQ1t, TQ1x);
  or SUB0O (TQj, B0, Bin);
  xor SUB2D (D2, TQu, TQy);
  or SUB3C (TQ1c, TQ16, TQ17);
  and SUB5A (TQ1k, TQ1h, TQ1i);
  not SUB7N (TQ1v, A7);
  and SUB0A (TQl, TQi, TQj);
  and SUB5B (TQ1l, B5, TQ1j);
  or SUB7O (TQ1w, B7, TQ1x);
  not SUB2N (TQw, A2);
  xor SUB4X (TQ18, A4, B4);
  and SUB0B (TQm, B0, Bin);
  or SUB2O (TQx, B2, TQy);
  xor SUB4D (D4, TQ18, TQ1c);
  or SUB5C (TQ1q, TQ1k, TQ1l);
  and SUB7A (TQ1y, TQ1v, TQ1w);
  or SUB0C (TQr, TQl, TQm);
  and SUB2A (TQz, TQw, TQx);
  xor SUB6X (TQ1m, A6, B6);
  and SUB7B (TQ1z, B7, TQ1x);
  not SUB4N (TQ1a, A4);
  xor SUB1X (TQn, A1, B1);
  and SUB2B (TQ10, B2, TQy);
  or SUB4O (TQ1b, B4, TQ1c);
  xor SUB6D (D6, TQ1m, TQ1q);
  or SUB7C (Bout, TQ1y, TQ1z);
  xor SUB1D (D1, TQn, TQr);
  or SUB2C (TQ15, TQz, TQ10);
  and SUB4A (TQ1d, TQ1a, TQ1b);
  not SUB6N (TQ1o, A6);
  not SUB1N (TQp, A1);
  xor SUB3X (TQ11, A3, B3);
  and SUB4B (TQ1e, B4, TQ1c);
  or SUB6O (TQ1p, B6, TQ1q);
  or SUB1O (TQq, B1, TQr);
  xor SUB3D (D3, TQ11, TQ15);
  or SUB4C (TQ1j, TQ1d, TQ1e);
  and SUB6A (TQ1r, TQ1o, TQ1p);
  and SUB1A (TQs, TQp, TQq);
  not SUB3N (TQ13, A3);
  xor SUB5X (TQ1f, A5, B5);
  and SUB6B (TQ1s, B6, TQ1q);

  // Other names for the same wires on the sheet: TQ0 = A0; TQ1 = B0; TQ1g = D5; TQ1n = D6; TQ1u = D7; TQ2 = A1;
  //   TQ3 = B1; TQ4 = A2; TQ5 = B2; TQ6 = A3; TQ7 = B3; TQ8 = A4; TQ9 = B4; TQ12 = D3; TQ19 = D4; TQ20 = Bout;
  //   TQa = A5; TQb = B5; TQc = A6; TQd = B6; TQe = A7; TQf = B7; TQh = D0; TQk = Bin; TQo = D1; TQv = D2
endmodule
