// Logisim project ttl_74138.circ as structural Verilog
module ttl_74138 (
  input  A,
  input  B,
  input  C,
  input  nG2A_Enable,
  input  nG2B_Enable,
  input  G1_Enable,
  output nY7,
  output nY6,
  output nY5,
  output nY4,
  output nY3,
  output nY2,
  output nY1,
  output nY0
);

  _74138 u_74138_1 (
    .pin1(A), .pin2(B), .pin3(C), .pin4(nG2A_Enable), .pin5(nG2B_Enable), .pin6(G1_Enable), .pin7(nY5),
    .pin15(B), .pin14(C), .pin13(nG2A_Enable), .pin12(nG2B_Enable), .pin11(G1_Enable), .pin10(nY5), .pin9(nY6));

  assign nY0 = B;
  assign nY1 = C;
  assign nY2 = nG2A_Enable;
  assign nY3 = nG2B_Enable;
  assign nY4 = G1_Enable;
  assign nY7 = nY5;
endmodule
