// Logisim project updown_counter_4bit.circ as structural Verilog
module updown_counter_4bit (
  input  CLK,
  input  UD,
  input  EN,
  input  RST,
  output Q0,
  output Q1,
  output Q2,
  output Q3
);

  wire TQ5, TQ8, TQ9, TQa, TQb, TQc, TQd, TQe, TQf, TQg, TQh, TQj, TQk, TQl, TQm;

  not N1 (TQg, UD);
  and TD2 (TQb, UD, TQe);
  T_Flip_Flop U1 (.T(EN), .clk(CLK), .Q(Q0), .reset(RST));  // open: Qn, preset
  or TO2 (TQc, TQa, TQb);
  not N2 (TQ8, Q0);
  and AU3 (TQh, TQd, Q2);
  T_Flip_Flop U2 (.T(TQ5), .clk(CLK), .Q(Q1), .reset(RST));  // open: Qn, preset
  and AD3 (TQj, TQe, TQf);
  not N3 (TQ9, Q1);
  and TU3 (TQk, TQg, TQh);
  T_Flip_Flop U3 (.T(TQc), .clk(CLK), .Q(Q2), .reset(RST));  // open: Qn, preset
  and TD3 (TQl, UD, TQj);
  not N4 (TQf, Q2);
  or TO3 (TQm, TQk, TQl);
  T_Flip_Flop U4 (.T(TQm), .clk(CLK), .Q(Q3), .reset(RST));  // open: Qn, preset
  xor X1 (TQ5, Q0, UD);
  and AU2 (TQd, Q0, Q1);
  and AD2 (TQe, TQ8, TQ9);
  and TU2 (TQa, TQg, TQd);

  // Other names for the same wires on the sheet: TQ0 = Q0; TQ1 = Q1; TQ2 = EN; TQ3 = Q2; TQ4 = CLK; TQ6 = RST;
  //   TQ7 = Q3; TQi = UD
endmodule
