// Logisim project vending_machine.circ as structural Verilog
module vending_machine (
  input  RST,
  input  A,
  input  B,
  output DONE
);

  wire A88_out, O90_out, O91_out, O92_out, O94_out, O95_out, O96_out, O97_out, O98_out, TQ0, TQ1a, TQ1b,
       TQ1c, TQ1d, TQ1e, TQ1f, TQ1g, TQ1h, TQ1i, TQ1j, TQ1k, TQ1l, TQ1m, TQ1n, TQ1o, TQ1p, TQ1q, TQ1r, TQ1s,
       TQ1t, TQ1u, TQ1v, TQ1w, TQ1x, TQ1y, TQ1z, TQ2, TQ2a, TQ2b, TQ2c, TQ2d, TQ2e, TQ2f, TQ2g, TQ2h, TQ2i,
       TQ2j, TQ3, TQ4, TQ5, TQ6, TQ7, TQ8, TQ9, TQ10, TQ11, TQ12, TQ13, TQ14, TQ15, TQ16, TQ17, TQ18, TQ19,
       TQ20, TQ21, TQ24, TQ25, TQ26, TQ27, TQ28, TQ29, TQa, TQb, TQc, TQd, TQe, TQf, TQg, TQh, TQi, TQj, TQk,
       TQl, TQm, TQn, TQo, TQp, TQq, TQr, TQs, TQt, TQu, TQv, TQw, TQx, TQy, TQz;

  Clock CLK (.out(TQ0));
  D_Flip_Flop U1 (.D(TQ26), .clk(TQ0), .Q(TQ1f), .reset(RST));  // open: Qn, preset
  D_Flip_Flop U2 (.D(TQ2e), .clk(TQ0), .Q(TQ1g), .reset(RST));  // open: Qn, preset
  D_Flip_Flop U3 (.D(TQ2h), .clk(TQ0), .Q(TQ20), .reset(RST));  // open: Qn, preset
  not N1 (TQ1x, TQ1f);
  not N2 (TQ1y, TQ1g);
  not N3 (TQ1i, TQ20);
  not NIa (TQ1w, A);
  not NIb (TQ1r, B);
  and M0 (TQ2, TQ1x, TQ1y);
  // AND_Gate M1 has open pins: in0=TQ2, in1=TQ1i, out=open
  and A2 (TQ3, TQ1x, TQ1y);
  and A3 (TQ4, TQ3, TQ1i);
  and A4 (TQ5, TQ4, TQ1r);
  // AND_Gate A5 has open pins: in0=TQ5, in1=TQ1w, out=open
  and A6 (TQ6, TQ1x, TQ1y);
  and A7 (TQ7, TQ6, TQ1i);
  and A8 (TQ8, TQ7, TQ1r);
  and A9 (TQ24, TQ8, A);
  and A10 (TQ9, TQ1x, TQ1y);
  and A11 (TQa, TQ9, TQ1i);
  and A12 (TQb, TQa, B);
  and A13 (TQ27, TQb, TQ1w);
  and A14 (TQc, TQ1x, TQ1y);
  and A15 (TQd, TQc, TQ1i);
  and A16 (TQe, TQd, B);
  and A17 (TQ28, TQe, A);
  and M18 (TQf, TQ1f, TQ1y);
  // AND_Gate M19 has open pins: in0=TQf, in1=TQ1i, out=open
  and A20 (TQg, TQ1f, TQ1y);
  and A21 (TQh, TQg, TQ1i);
  and A22 (TQi, TQh, TQ1r);
  and A23 (TQ25, TQi, TQ1w);
  and A24 (TQj, TQ1f, TQ1y);
  and A25 (TQk, TQj, TQ1i);
  and A26 (TQl, TQk, TQ1r);
  and A27 (TQ29, TQl, A);
  and A28 (TQm, TQ1f, TQ1y);
  and A29 (TQn, TQm, TQ1i);
  and A30 (TQo, TQn, B);
  and A31 (TQ2b, TQo, TQ1w);
  and A32 (TQp, TQ1f, TQ1y);
  and A33 (TQq, TQp, TQ1i);
  and A34 (TQr, TQq, B);
  and A35 (TQ2c, TQr, A);
  and M36 (TQs, TQ1x, TQ1g);
  // AND_Gate M37 has open pins: in0=TQs, in1=TQ1i, out=open
  and A38 (TQt, TQ1x, TQ1g);
  and A39 (TQu, TQt, TQ1i);
  and A40 (TQv, TQu, TQ1r);
  and A41 (TQ2a, TQv, TQ1w);
  and A42 (TQw, TQ1x, TQ1g);
  and A43 (TQx, TQw, TQ1i);
  and A44 (TQy, TQx, TQ1r);
  and A45 (TQ2d, TQy, A);
  and A46 (TQz, TQ1x, TQ1g);
  and A47 (TQ10, TQz, TQ1i);
  and A48 (TQ11, TQ10, B);
  and A49 (TQ2f, TQ11, TQ1w);
  and A50 (TQ12, TQ1x, TQ1g);
  and A51 (TQ13, TQ12, TQ1i);
  and A52 (TQ14, TQ13, B);
  and A53 (TQ2g, TQ14, A);
  and M54 (TQ15, TQ1f, TQ1g);
  and M55 (TQ2i, TQ15, TQ1i);
  and A56 (TQ16, TQ1f, TQ1g);
  and A57 (TQ17, TQ16, TQ1i);
  and A58 (TQ18, TQ17, TQ1r);
  // AND_Gate A59 has open pins: in0=TQ18, in1=TQ1w, out=open
  and A60 (TQ19, TQ1f, TQ1g);
  and A61 (TQ1a, TQ19, TQ1i);
  and A62 (TQ1b, TQ1a, TQ1r);
  // AND_Gate A63 has open pins: in0=TQ1b, in1=A, out=open
  and A64 (TQ1c, TQ1f, TQ1g);
  and A65 (TQ1d, TQ1c, TQ1i);
  and A66 (TQ1e, TQ1d, B);
  // AND_Gate A67 has open pins: in0=TQ1e, in1=TQ1w, out=open
  and A68 (TQ1h, TQ1f, TQ1g);
  and A69 (TQ1j, TQ1h, TQ1i);
  and A70 (TQ1k, TQ1j, B);
  // AND_Gate A71 has open pins: in0=TQ1k, in1=A, out=open
  and M72 (TQ1l, TQ1x, TQ1y);
  and M73 (TQ2j, TQ1l, TQ20);
  and A74 (TQ1m, TQ1x, TQ1y);
  and A75 (TQ1n, TQ1m, TQ20);
  and A76 (TQ1o, TQ1n, TQ1r);
  // AND_Gate A77 has open pins: in0=TQ1o, in1=TQ1w, out=open
  and A78 (TQ1p, TQ1x, TQ1y);
  and A79 (TQ1q, TQ1p, TQ20);
  and A80 (TQ1s, TQ1q, TQ1r);
  // AND_Gate A81 has open pins: in0=TQ1s, in1=A, out=open
  and A82 (TQ1t, TQ1x, TQ1y);
  and A83 (TQ1u, TQ1t, TQ20);
  and A84 (TQ1v, TQ1u, B);
  // AND_Gate A85 has open pins: in0=TQ1v, in1=TQ1w, out=open
  and A86 (TQ1z, TQ1x, TQ1y);
  and A87 (TQ21, TQ1z, TQ20);
  and A88 (A88_out, TQ21, B);
  // AND_Gate A89 has open pins: in0=A88_out, in1=A, out=open
  or O90 (O90_out, TQ24, TQ25);
  or O91 (O91_out, O90_out, TQ2b);
  or O92 (O92_out, O91_out, TQ2c);
  or O93 (TQ26, O92_out, TQ2d);
  or O94 (O94_out, TQ27, TQ28);
  or O95 (O95_out, O94_out, TQ29);
  or O96 (O96_out, O95_out, TQ2a);
  or O97 (O97_out, O96_out, TQ2b);
  or O98 (O98_out, O97_out, TQ2c);
  or O99 (TQ2e, O98_out, TQ2d);
  or O100 (TQ2h, TQ2f, TQ2g);
  or Ofo101 (DONE, TQ2i, TQ2j);

  // Other names for the same wires on the sheet: TQ1 = RST; TQ2k = DONE; TQ22 = B; TQ23 = A
endmodule
